// Logisim project 16 bit computer.circ as structural Verilog
module BUS_Register (
  input  [15:0] DataIn,
  input  Instruction_Enable,
  input  CLK,
  input  [2:0] Instruction_Line,
  output [15:0] DataOut
);

  wire and_1_out, and_2_out, and_3_out, and_4_out, and_5_out, and_6_out, and_7_out, and_8_out, and_9_out,
       counter_1_carry, decoder_1_out0, decoder_1_out1, decoder_1_out2, decoder_1_out3, decoder_1_out4,
       decoder_1_out5, decoder_1_out6, not_1_out, not_2_out, or_1_out, or_2_out, or_3_out, or_4_out;
  wire [7:0] counter_1_q, counter_2_q, multiplexer_1_out;
  wire [15:0] controlled_buffer_1_out;

  Decoder #(.select(3), .enable("false")) decoder_1 (
    .out0(decoder_1_out0), .out1(decoder_1_out1), .out2(decoder_1_out2), .out3(decoder_1_out3),
    .out4(decoder_1_out4), .out5(decoder_1_out5), .out6(decoder_1_out6), .sel(Instruction_Line));  // open: out7
  and and_1 (and_1_out, decoder_1_out0, Instruction_Enable);
  and and_2 (and_2_out, decoder_1_out1, Instruction_Enable);
  and and_3 (and_3_out, decoder_1_out2, Instruction_Enable);
  and and_4 (and_4_out, decoder_1_out3, Instruction_Enable);
  and and_5 (and_5_out, decoder_1_out4, Instruction_Enable);
  and and_6 (and_6_out, decoder_1_out5, Instruction_Enable);
  and and_7 (and_7_out, decoder_1_out6, Instruction_Enable);
  assign controlled_buffer_1_out = not_1_out ? DataIn : 16'bz;  // Controlled_Buffer controlled_buffer_1
  not not_1 (not_1_out, and_7_out);
  or or_1 (or_1_out, and_4_out, and_1_out, and_3_out);
  or or_2 (or_2_out, and_8_out, and_1_out, and_2_out);
  not not_2 (not_2_out, and_2_out);
  or or_3 (or_3_out, and_4_out, and_5_out);
  Multiplexer #(.width(8)) multiplexer_1 (
    .in0(controlled_buffer_1_out[7:0]), .in1(controlled_buffer_1_out[15:8]), .out(multiplexer_1_out),
    .sel(not_2_out), .en(1'b1));
  Counter counter_1 (
    .load(or_1_out), .D(controlled_buffer_1_out[7:0]), .count(or_3_out), .Q(counter_1_q),
    .carry(counter_1_carry), .clk(CLK), .clr(and_6_out));
  Counter counter_2 (
    .load(or_2_out), .D(multiplexer_1_out), .count(or_4_out), .Q(counter_2_q), .clk(CLK), .clr(and_6_out));  // open: carry
  and and_8 (and_8_out, counter_1_carry, and_4_out);
  and and_9 (and_9_out, counter_1_carry, ~or_2_out, ~and_7_out, Instruction_Enable);  // AND_Gate
  or or_4 (or_4_out, and_9_out, and_8_out);
  assign DataOut = and_7_out ? {counter_2_q, counter_1_q} : 16'bz;  // Controlled_Buffer controlled_buffer_2

  // Notes on the sheet:
  //   mov reg,value16
  //   mov regH,value8
  //   mov regL,value8
  //   dec reg
  //   inc reg
  //   set 0
  //   Read/Write
endmodule

module BUS_ALU (
  input  [15:0] BUS_In,
  input  Read_Write,
  input  CLK,
  input  Load_Enable,
  input  Load_Selector,
  input  Add_Sub,
  output [15:0] BUS_Out
);

  wire and_1_out, and_2_out, not_1_out;
  wire [15:0] adder_1_out, controlled_buffer_2_out, multiplexer_1_out, register_1_q, register_2_q,
       subtractor_1_out;

  assign BUS_Out = Read_Write ? multiplexer_1_out : 16'bz;  // Controlled_Buffer controlled_buffer_1
  assign controlled_buffer_2_out = not_1_out ? BUS_In : 16'bz;  // Controlled_Buffer controlled_buffer_2
  not not_1 (not_1_out, Read_Write);
  and and_1 (and_1_out, Load_Selector, Load_Enable);
  Register #(.width(16)) register_1 (
    .D(controlled_buffer_2_out), .en(and_1_out), .Q(register_1_q), .clk(CLK));  // open: clr
  Register #(.width(16)) register_2 (
    .D(controlled_buffer_2_out), .en(and_2_out), .Q(register_2_q), .clk(CLK));  // open: clr
  and and_2 (and_2_out, Load_Enable, ~Load_Selector);  // AND_Gate
  Adder #(.width(16)) adder_1 (.a(register_1_q), .b(register_2_q), .out(adder_1_out));  // open: cin, cout
  Subtractor #(.width(16)) subtractor_1 (
    .a(register_1_q), .b(register_2_q), .out(subtractor_1_out));  // open: bin, bout
  Multiplexer #(.width(16)) multiplexer_1 (
    .in0(adder_1_out), .in1(subtractor_1_out), .out(multiplexer_1_out), .sel(Add_Sub), .en(1'b1));
endmodule

module BUS_RAM (
  input  [15:0] Bus_In,
  input  CLK,
  input  [7:0] RAM_Instruction,
  input  RAM_Instruction_Enable,
  output [15:0] Bus_Out
);

  wire Inc_Address_out, jmp__data_out, Load_Temp_Address_out, mov_ip__ip_out, or_1_out, or_2_out, or_3_out,
       Read_To_BUS_At_IP_out, Read_Write_out, Store_at_IP_out, Use_Instruction_Pointer_Use_Temp_Address_out;
  wire [15:0] controlled_buffer_2_out, Instruction_Pointer_q, multiplexer_1_out, ram_1_data,
       Temp_Address_Pointer_q;

  and jmp__data (jmp__data_out, RAM_Instruction_Enable, RAM_Instruction[0]);
  and mov_ip__ip (mov_ip__ip_out, RAM_Instruction_Enable, RAM_Instruction[1]);
  and Store_at_IP (Store_at_IP_out, RAM_Instruction_Enable, RAM_Instruction[2]);
  and Read_To_BUS_At_IP (Read_To_BUS_At_IP_out, RAM_Instruction_Enable, RAM_Instruction[3]);
  and Read_Write (Read_Write_out, RAM_Instruction_Enable, RAM_Instruction[4]);
  and Inc_Address (Inc_Address_out, RAM_Instruction_Enable, RAM_Instruction[5]);
  and Load_Temp_Address (Load_Temp_Address_out, RAM_Instruction_Enable, RAM_Instruction[6]);
  nand Use_Instruction_Pointer_Use_Temp_Address (Use_Instruction_Pointer_Use_Temp_Address_out, RAM_Instruction_Enable, RAM_Instruction[7]);
  assign Bus_Out = Read_Write_out ? ram_1_data : 16'bz;  // Controlled_Buffer controlled_buffer_1
  assign controlled_buffer_2_out = mov_ip__ip_out ? ram_1_data : 16'bz;  // Controlled_Buffer controlled_buffer_2
  assign controlled_buffer_2_out = or_1_out ? Bus_In : 16'bz;  // Controlled_Buffer controlled_buffer_3
  or or_1 (or_1_out, Store_at_IP_out, Load_Temp_Address_out, jmp__data_out);
  Register #(.width(16)) Temp_Address_Pointer (
    .D(controlled_buffer_2_out), .en(Load_Temp_Address_out), .Q(Temp_Address_Pointer_q), .clk(CLK));  // open: clr
  or or_2 (or_2_out, jmp__data_out, mov_ip__ip_out);
  Counter #(.width(16), .max('hffff)) Instruction_Pointer (
    .load(or_2_out), .D(controlled_buffer_2_out), .count(Inc_Address_out), .Q(Instruction_Pointer_q),
    .clk(CLK));  // open: carry, clr
  Multiplexer #(.width(16), .enable("false")) multiplexer_1 (
    .in0(Temp_Address_Pointer_q), .in1(Instruction_Pointer_q), .out(multiplexer_1_out),
    .sel(Use_Instruction_Pointer_Use_Temp_Address_out));
  or or_3 (or_3_out, mov_ip__ip_out, Read_To_BUS_At_IP_out);
  RAM #(.addrWidth(16), .dataWidth(16), .bus("separate")) ram_1 (
    .addr(multiplexer_1_out), .din(controlled_buffer_2_out), .data(ram_1_data), .str(Store_at_IP_out),
    .clk(CLK), .ld(or_3_out));  // open: sel, clr
endmodule

module BUS_GPU (
  input  [15:0] Bus_In,
  input  CLK,
  input  Set_Pixel_Bank,
  input  Bank_Selector,
  output [15:0] Bus_Out
);

  wire and_1_out, decoder_1_out0, decoder_1_out1, decoder_1_out2, decoder_1_out3, decoder_1_out4,
       decoder_1_out5, decoder_1_out6, decoder_1_out7, decoder_1_out8, decoder_1_out9, decoder_1_out10,
       decoder_1_out11, decoder_1_out12, decoder_1_out13, decoder_1_out14, decoder_1_out15, decoder_1_out16,
       decoder_1_out17, decoder_1_out18, decoder_1_out19, decoder_1_out20, decoder_1_out21, decoder_1_out22,
       decoder_1_out23, decoder_1_out24, decoder_1_out25, decoder_1_out26, decoder_1_out27, decoder_1_out28,
       decoder_1_out29, decoder_1_out30, decoder_1_out31, decoder_2_out0, decoder_2_out1, decoder_2_out2,
       decoder_2_out3, decoder_2_out4, decoder_2_out5, decoder_2_out6, decoder_2_out7, decoder_2_out8,
       decoder_2_out9, decoder_2_out10, decoder_2_out11, decoder_2_out12, decoder_2_out13, decoder_2_out14,
       decoder_2_out15, decoder_2_out16, decoder_2_out17, decoder_2_out18, decoder_2_out19, decoder_2_out20,
       decoder_2_out21, decoder_2_out22, decoder_2_out23, decoder_2_out24, decoder_2_out25, decoder_2_out26,
       decoder_2_out27, decoder_2_out28, decoder_2_out29, decoder_2_out30, decoder_2_out31, undriven;
  wire [4:0] controlled_buffer_2_out, register_1_q, register_2_q;
  wire [15:0] undriven_2;
  wire [15:5] controlled_buffer_2_out_2;
  wire [31:0] bus_gpu_register_1_out_5, bus_gpu_register_2_out_5, bus_gpu_register_3_out_5,
       bus_gpu_register_4_out_5, bus_gpu_register_5_out_5, bus_gpu_register_6_out_5,
       bus_gpu_register_7_out_5, bus_gpu_register_8_out_5, bus_gpu_register_9_out_5,
       bus_gpu_register_10_out_5, bus_gpu_register_11_out_5, bus_gpu_register_12_out_5,
       bus_gpu_register_13_out_5, bus_gpu_register_14_out_5, bus_gpu_register_15_out_5,
       bus_gpu_register_16_out_5, bus_gpu_register_17_out_5, bus_gpu_register_18_out_5,
       bus_gpu_register_19_out_5, bus_gpu_register_20_out_5, bus_gpu_register_21_out_5,
       bus_gpu_register_22_out_5, bus_gpu_register_23_out_5, bus_gpu_register_24_out_5,
       bus_gpu_register_25_out_5, bus_gpu_register_26_out_5, bus_gpu_register_27_out_5,
       bus_gpu_register_28_out_5, bus_gpu_register_29_out_5, bus_gpu_register_30_out_5,
       bus_gpu_register_31_out_5, bus_gpu_register_32_out_5;

  assign Bus_Out = undriven ? undriven_2 : 16'bz;  // Controlled_Buffer controlled_buffer_1
  assign {controlled_buffer_2_out_2, controlled_buffer_2_out} = Set_Pixel_Bank ? Bus_In : 16'bz;  // Controlled_Buffer controlled_buffer_2
  Register #(.width(5)) register_1 (
    .D(controlled_buffer_2_out), .en(Bank_Selector), .Q(register_1_q), .clk(CLK));  // open: clr
  Decoder #(.select(5), .enable("false")) decoder_1 (
    .out0(decoder_1_out0), .out1(decoder_1_out1), .out2(decoder_1_out2), .out3(decoder_1_out3),
    .out4(decoder_1_out4), .out5(decoder_1_out5), .out6(decoder_1_out6), .out7(decoder_1_out7),
    .out8(decoder_1_out8), .out9(decoder_1_out9), .out10(decoder_1_out10), .out11(decoder_1_out11),
    .out12(decoder_1_out12), .out13(decoder_1_out13), .out14(decoder_1_out14), .out15(decoder_1_out15),
    .out16(decoder_1_out16), .out17(decoder_1_out17), .out18(decoder_1_out18), .out19(decoder_1_out19),
    .out20(decoder_1_out20), .out21(decoder_1_out21), .out22(decoder_1_out22), .out23(decoder_1_out23),
    .out24(decoder_1_out24), .out25(decoder_1_out25), .out26(decoder_1_out26), .out27(decoder_1_out27),
    .out28(decoder_1_out28), .out29(decoder_1_out29), .out30(decoder_1_out30), .out31(decoder_1_out31),
    .sel(register_1_q));
  and and_1 (and_1_out, Set_Pixel_Bank, ~Bank_Selector);  // AND_Gate
  Register #(.width(5)) register_2 (
    .D(controlled_buffer_2_out), .en(and_1_out), .Q(register_2_q), .clk(CLK));  // open: clr
  Decoder #(.select(5), .enable("false")) decoder_2 (
    .out0(decoder_2_out0), .out1(decoder_2_out1), .out2(decoder_2_out2), .out3(decoder_2_out3),
    .out4(decoder_2_out4), .out5(decoder_2_out5), .out6(decoder_2_out6), .out7(decoder_2_out7),
    .out8(decoder_2_out8), .out9(decoder_2_out9), .out10(decoder_2_out10), .out11(decoder_2_out11),
    .out12(decoder_2_out12), .out13(decoder_2_out13), .out14(decoder_2_out14), .out15(decoder_2_out15),
    .out16(decoder_2_out16), .out17(decoder_2_out17), .out18(decoder_2_out18), .out19(decoder_2_out19),
    .out20(decoder_2_out20), .out21(decoder_2_out21), .out22(decoder_2_out22), .out23(decoder_2_out23),
    .out24(decoder_2_out24), .out25(decoder_2_out25), .out26(decoder_2_out26), .out27(decoder_2_out27),
    .out28(decoder_2_out28), .out29(decoder_2_out29), .out30(decoder_2_out30), .out31(decoder_2_out31),
    .sel(register_2_q));
  DotMatrix #(.matrixcols(32), .matrixrows(32)) dotmatrix_1 (
    .col0(bus_gpu_register_1_out_5), .col1(bus_gpu_register_2_out_5), .col2(bus_gpu_register_3_out_5),
    .col3(bus_gpu_register_4_out_5), .col4(bus_gpu_register_5_out_5), .col5(bus_gpu_register_6_out_5),
    .col6(bus_gpu_register_7_out_5), .col7(bus_gpu_register_8_out_5), .col8(bus_gpu_register_9_out_5),
    .col9(bus_gpu_register_10_out_5), .col10(bus_gpu_register_11_out_5), .col11(bus_gpu_register_12_out_5),
    .col12(bus_gpu_register_13_out_5), .col13(bus_gpu_register_14_out_5), .col14(bus_gpu_register_15_out_5),
    .col15(bus_gpu_register_16_out_5), .col16(bus_gpu_register_17_out_5), .col17(bus_gpu_register_18_out_5),
    .col18(bus_gpu_register_19_out_5), .col19(bus_gpu_register_20_out_5), .col20(bus_gpu_register_21_out_5),
    .col21(bus_gpu_register_22_out_5), .col22(bus_gpu_register_23_out_5), .col23(bus_gpu_register_24_out_5),
    .col24(bus_gpu_register_25_out_5), .col25(bus_gpu_register_26_out_5), .col26(bus_gpu_register_27_out_5),
    .col27(bus_gpu_register_28_out_5), .col28(bus_gpu_register_29_out_5), .col29(bus_gpu_register_30_out_5),
    .col30(bus_gpu_register_31_out_5), .col31(bus_gpu_register_32_out_5));
  BUS_GPU_Register bus_gpu_register_1 (
    .Data_In({controlled_buffer_2_out_2, controlled_buffer_2_out}), .CLK(CLK), .Write_Enable(decoder_1_out0),
    .Write_Select(decoder_2_out0), .out_5(bus_gpu_register_1_out_5));
  BUS_GPU_Register bus_gpu_register_2 (
    .Data_In({controlled_buffer_2_out_2, controlled_buffer_2_out}), .CLK(CLK), .Write_Enable(decoder_1_out1),
    .Write_Select(decoder_2_out1), .out_5(bus_gpu_register_2_out_5));
  BUS_GPU_Register bus_gpu_register_3 (
    .Data_In({controlled_buffer_2_out_2, controlled_buffer_2_out}), .CLK(CLK), .Write_Enable(decoder_1_out2),
    .Write_Select(decoder_2_out2), .out_5(bus_gpu_register_3_out_5));
  BUS_GPU_Register bus_gpu_register_4 (
    .Data_In({controlled_buffer_2_out_2, controlled_buffer_2_out}), .CLK(CLK), .Write_Enable(decoder_1_out3),
    .Write_Select(decoder_2_out3), .out_5(bus_gpu_register_4_out_5));
  BUS_GPU_Register bus_gpu_register_5 (
    .Data_In({controlled_buffer_2_out_2, controlled_buffer_2_out}), .CLK(CLK), .Write_Enable(decoder_1_out4),
    .Write_Select(decoder_2_out4), .out_5(bus_gpu_register_5_out_5));
  BUS_GPU_Register bus_gpu_register_6 (
    .Data_In({controlled_buffer_2_out_2, controlled_buffer_2_out}), .CLK(CLK), .Write_Enable(decoder_1_out5),
    .Write_Select(decoder_2_out5), .out_5(bus_gpu_register_6_out_5));
  BUS_GPU_Register bus_gpu_register_7 (
    .Data_In({controlled_buffer_2_out_2, controlled_buffer_2_out}), .CLK(CLK), .Write_Enable(decoder_1_out6),
    .Write_Select(decoder_2_out6), .out_5(bus_gpu_register_7_out_5));
  BUS_GPU_Register bus_gpu_register_8 (
    .Data_In({controlled_buffer_2_out_2, controlled_buffer_2_out}), .CLK(CLK), .Write_Enable(decoder_1_out7),
    .Write_Select(decoder_2_out7), .out_5(bus_gpu_register_8_out_5));
  BUS_GPU_Register bus_gpu_register_9 (
    .Data_In({controlled_buffer_2_out_2, controlled_buffer_2_out}), .CLK(CLK), .Write_Enable(decoder_1_out8),
    .Write_Select(decoder_2_out8), .out_5(bus_gpu_register_9_out_5));
  BUS_GPU_Register bus_gpu_register_10 (
    .Data_In({controlled_buffer_2_out_2, controlled_buffer_2_out}), .CLK(CLK), .Write_Enable(decoder_1_out9),
    .Write_Select(decoder_2_out9), .out_5(bus_gpu_register_10_out_5));
  BUS_GPU_Register bus_gpu_register_11 (
    .Data_In({controlled_buffer_2_out_2, controlled_buffer_2_out}), .CLK(CLK),
    .Write_Enable(decoder_1_out10), .Write_Select(decoder_2_out10), .out_5(bus_gpu_register_11_out_5));
  BUS_GPU_Register bus_gpu_register_12 (
    .Data_In({controlled_buffer_2_out_2, controlled_buffer_2_out}), .CLK(CLK),
    .Write_Enable(decoder_1_out11), .Write_Select(decoder_2_out11), .out_5(bus_gpu_register_12_out_5));
  BUS_GPU_Register bus_gpu_register_13 (
    .Data_In({controlled_buffer_2_out_2, controlled_buffer_2_out}), .CLK(CLK),
    .Write_Enable(decoder_1_out12), .Write_Select(decoder_2_out12), .out_5(bus_gpu_register_13_out_5));
  BUS_GPU_Register bus_gpu_register_14 (
    .Data_In({controlled_buffer_2_out_2, controlled_buffer_2_out}), .CLK(CLK),
    .Write_Enable(decoder_1_out13), .Write_Select(decoder_2_out13), .out_5(bus_gpu_register_14_out_5));
  BUS_GPU_Register bus_gpu_register_15 (
    .Data_In({controlled_buffer_2_out_2, controlled_buffer_2_out}), .CLK(CLK),
    .Write_Enable(decoder_1_out14), .Write_Select(decoder_2_out14), .out_5(bus_gpu_register_15_out_5));
  BUS_GPU_Register bus_gpu_register_16 (
    .Data_In({controlled_buffer_2_out_2, controlled_buffer_2_out}), .CLK(CLK),
    .Write_Enable(decoder_1_out15), .Write_Select(decoder_2_out15), .out_5(bus_gpu_register_16_out_5));
  BUS_GPU_Register bus_gpu_register_17 (
    .Data_In({controlled_buffer_2_out_2, controlled_buffer_2_out}), .CLK(CLK),
    .Write_Enable(decoder_1_out16), .Write_Select(decoder_2_out16), .out_5(bus_gpu_register_17_out_5));
  BUS_GPU_Register bus_gpu_register_18 (
    .Data_In({controlled_buffer_2_out_2, controlled_buffer_2_out}), .CLK(CLK),
    .Write_Enable(decoder_1_out17), .Write_Select(decoder_2_out17), .out_5(bus_gpu_register_18_out_5));
  BUS_GPU_Register bus_gpu_register_19 (
    .Data_In({controlled_buffer_2_out_2, controlled_buffer_2_out}), .CLK(CLK),
    .Write_Enable(decoder_1_out18), .Write_Select(decoder_2_out18), .out_5(bus_gpu_register_19_out_5));
  BUS_GPU_Register bus_gpu_register_20 (
    .Data_In({controlled_buffer_2_out_2, controlled_buffer_2_out}), .CLK(CLK),
    .Write_Enable(decoder_1_out19), .Write_Select(decoder_2_out19), .out_5(bus_gpu_register_20_out_5));
  BUS_GPU_Register bus_gpu_register_21 (
    .Data_In({controlled_buffer_2_out_2, controlled_buffer_2_out}), .CLK(CLK),
    .Write_Enable(decoder_1_out20), .Write_Select(decoder_2_out20), .out_5(bus_gpu_register_21_out_5));
  BUS_GPU_Register bus_gpu_register_22 (
    .Data_In({controlled_buffer_2_out_2, controlled_buffer_2_out}), .CLK(CLK),
    .Write_Enable(decoder_1_out21), .Write_Select(decoder_2_out21), .out_5(bus_gpu_register_22_out_5));
  BUS_GPU_Register bus_gpu_register_23 (
    .Data_In({controlled_buffer_2_out_2, controlled_buffer_2_out}), .CLK(CLK),
    .Write_Enable(decoder_1_out22), .Write_Select(decoder_2_out22), .out_5(bus_gpu_register_23_out_5));
  BUS_GPU_Register bus_gpu_register_24 (
    .Data_In({controlled_buffer_2_out_2, controlled_buffer_2_out}), .CLK(CLK),
    .Write_Enable(decoder_1_out23), .Write_Select(decoder_2_out23), .out_5(bus_gpu_register_24_out_5));
  BUS_GPU_Register bus_gpu_register_25 (
    .Data_In({controlled_buffer_2_out_2, controlled_buffer_2_out}), .CLK(CLK),
    .Write_Enable(decoder_1_out24), .Write_Select(decoder_2_out24), .out_5(bus_gpu_register_25_out_5));
  BUS_GPU_Register bus_gpu_register_26 (
    .Data_In({controlled_buffer_2_out_2, controlled_buffer_2_out}), .CLK(CLK),
    .Write_Enable(decoder_1_out25), .Write_Select(decoder_2_out25), .out_5(bus_gpu_register_26_out_5));
  BUS_GPU_Register bus_gpu_register_27 (
    .Data_In({controlled_buffer_2_out_2, controlled_buffer_2_out}), .CLK(CLK),
    .Write_Enable(decoder_1_out26), .Write_Select(decoder_2_out26), .out_5(bus_gpu_register_27_out_5));
  BUS_GPU_Register bus_gpu_register_28 (
    .Data_In({controlled_buffer_2_out_2, controlled_buffer_2_out}), .CLK(CLK),
    .Write_Enable(decoder_1_out27), .Write_Select(decoder_2_out27), .out_5(bus_gpu_register_28_out_5));
  BUS_GPU_Register bus_gpu_register_29 (
    .Data_In({controlled_buffer_2_out_2, controlled_buffer_2_out}), .CLK(CLK),
    .Write_Enable(decoder_1_out28), .Write_Select(decoder_2_out28), .out_5(bus_gpu_register_29_out_5));
  BUS_GPU_Register bus_gpu_register_30 (
    .Data_In({controlled_buffer_2_out_2, controlled_buffer_2_out}), .CLK(CLK),
    .Write_Enable(decoder_1_out29), .Write_Select(decoder_2_out29), .out_5(bus_gpu_register_30_out_5));
  BUS_GPU_Register bus_gpu_register_31 (
    .Data_In({controlled_buffer_2_out_2, controlled_buffer_2_out}), .CLK(CLK),
    .Write_Enable(decoder_1_out30), .Write_Select(decoder_2_out30), .out_5(bus_gpu_register_31_out_5));
  BUS_GPU_Register bus_gpu_register_32 (
    .Data_In({controlled_buffer_2_out_2, controlled_buffer_2_out}), .CLK(CLK),
    .Write_Enable(decoder_1_out31), .Write_Select(decoder_2_out31), .out_5(bus_gpu_register_32_out_5));
endmodule

module BUS_GPU_Register (
  input  [15:0] Data_In,
  input  CLK,
  input  Write_Enable,
  input  Write_Select,
  output [31:0] out_5
);

  wire and_1_out, and_2_out;

  and and_1 (and_1_out, Write_Enable, ~Write_Select);  // AND_Gate
  and and_2 (and_2_out, Write_Enable, Write_Select);
  Register #(.width(16)) register_1 (.D(Data_In), .en(and_1_out), .Q(out_5[15:0]), .clk(CLK));  // open: clr
  Register #(.width(16)) register_2 (.D(Data_In), .en(and_2_out), .Q(out_5[31:16]), .clk(CLK));  // open: clr
endmodule

module BUS_Math_Unit (
  input  [15:0] BUS_IN,
  input  [3:0] Instruction,
  input  Enable,
  input  CLK,
  output [15:0] BUS_OUT
);

  wire and_1_out, and_2_out;
  wire [15:0] adder_1_out, register_1_q, register_2_q, subtractor_1_out;

  Register #(.width(16)) register_1 (.D(BUS_IN), .en(and_1_out), .Q(register_1_q), .clk(CLK));  // open: clr
  and and_1 (and_1_out, ~Instruction[0], Instruction[3], Enable);  // AND_Gate
  Register #(.width(16)) register_2 (.D(BUS_IN), .en(and_2_out), .Q(register_2_q), .clk(CLK));  // open: clr
  and and_2 (and_2_out, Instruction[0], Instruction[3], Enable);
  Adder #(.width(16)) adder_1 (.a(register_1_q), .b(register_2_q), .out(adder_1_out));  // open: cin, cout
  Subtractor #(.width(16)) subtractor_1 (
    .a(register_1_q), .b(register_2_q), .out(subtractor_1_out));  // open: bin, bout
  Multiplexer #(.width(16)) multiplexer_1 (
    .in0(adder_1_out), .in1(subtractor_1_out), .out(BUS_OUT), .sel(Instruction[1]), .en(Instruction[2]));
endmodule

module BUS_Comparator (
  input  [15:0] Data_In,
  input  CLK,
  input  Enable,
  input  Instruction,
  output [1:0] Comparison_Line
);

  wire and_1_out, and_2_out, Equal_out, Greater_out, Less_out, subtractor_1_bout, subtractor_2_bout;
  wire [15:0] register_1_q, register_2_q, subtractor_1_out, subtractor_2_out;

  or or_1 (Comparison_Line[0], Equal_out, Less_out);
  or or_2 (Comparison_Line[1], Equal_out, Greater_out);
  Register #(.width(16)) register_1 (.D(Data_In), .en(and_1_out), .Q(register_1_q), .clk(CLK));  // open: clr
  and and_1 (and_1_out, ~Instruction, Enable);  // AND_Gate
  Register #(.width(16)) register_2 (.D(Data_In), .en(and_2_out), .Q(register_2_q), .clk(CLK));  // open: clr
  and and_2 (and_2_out, Instruction, Enable);
  and Equal (Equal_out, ~subtractor_1_bout, ~subtractor_2_bout);  // AND_Gate
  and Greater (Greater_out, ~subtractor_1_bout, subtractor_2_bout);  // AND_Gate
  and Less (Less_out, subtractor_1_bout, subtractor_2_bout);
  Subtractor #(.width(16)) subtractor_1 (
    .a(register_1_q), .b(register_2_q), .out(subtractor_1_out), .bout(subtractor_1_bout));  // open: bin
  // Probe on subtractor_1_out
  // Probe on subtractor_2_out
  Subtractor #(.width(16)) subtractor_2 (
    .a({16{1'b0}}), .b(subtractor_1_out), .out(subtractor_2_out), .bout(subtractor_2_bout));  // open: bin
endmodule

module Command_Unit_CMP_Instruction (
  input  CLK,
  input  Enable,
  output Running_Instruction,
  output Comparison_Enable,
  output Comparison_Instruction,
  output Base_Register_Enable,
  output [2:0] Base_Register_Instruction,
  output Other_Register_Enable,
  output [2:0] Other_Register_Instruction,
  output RAM_Enable,
  output [7:0] RAM_Instruction
);

  wire d_ff_1_qn, d_ff_2_qn, d_ff_3_qn;

  D_Flip_Flop d_ff_1 (.clk(CLK), .D(Enable), .Q(Base_Register_Enable), .Qn(d_ff_1_qn));  // open: preset, en, reset
  D_Flip_Flop d_ff_2 (
    .clk(CLK), .D(Base_Register_Enable), .Q(Comparison_Instruction), .Qn(d_ff_2_qn));  // open: preset, en, reset
  D_Flip_Flop d_ff_3 (
    .clk(CLK), .D(Comparison_Instruction), .Q(RAM_Enable), .Qn(d_ff_3_qn));  // open: preset, en, reset
  and and_1 (Running_Instruction, d_ff_3_qn, d_ff_2_qn, d_ff_1_qn);
  or or_1 (Comparison_Enable, Base_Register_Enable, Comparison_Instruction);

  assign Base_Register_Instruction = {{2{Base_Register_Enable}}, 1'b0};
  assign Other_Register_Enable = Comparison_Instruction;
  assign Other_Register_Instruction = {{2{Comparison_Instruction}}, 1'b0};
  assign RAM_Instruction = {2'b00, RAM_Enable, {5{1'b0}}};
endmodule

module Command_Unit_mov_reg_value16 (
  input  CLK,
  input  Enable,
  output Instruction_Running,
  output RAM_Enable,
  output Register_Enable,
  output [7:0] RAM_Instruction,
  output [2:0] Register_Instruction
);

  wire d_ff_1_q, d_ff_1_qn, d_ff_2_qn, d_ff_3_q, d_ff_3_qn;

  D_Flip_Flop d_ff_1 (.clk(CLK), .D(Enable), .Q(d_ff_1_q), .Qn(d_ff_1_qn));  // open: preset, en, reset
  D_Flip_Flop d_ff_2 (.clk(CLK), .D(d_ff_1_q), .Q(RAM_Instruction[4]), .Qn(d_ff_2_qn));  // open: preset, en, reset
  D_Flip_Flop d_ff_3 (.clk(CLK), .D(RAM_Instruction[4]), .Q(d_ff_3_q), .Qn(d_ff_3_qn));  // open: preset, en, reset
  or or_1 (RAM_Instruction[5], d_ff_3_q, d_ff_1_q);
  and and_1 (Instruction_Running, d_ff_3_qn, d_ff_2_qn, d_ff_1_qn);
  or or_2 (RAM_Enable, d_ff_3_q, d_ff_1_q);

  assign {RAM_Instruction[7:6], RAM_Instruction[3:0]} = {2'b00, RAM_Instruction[4], 3'b000};
  assign Register_Enable = RAM_Instruction[4];
  assign Register_Instruction = 3'b000;
endmodule

module Command_Unit_mov_reg_reg (
  input  CLK,
  input  Enable,
  output Instruction_Running,
  output RAM_Enable,
  output Destination_Enable,
  output [7:0] RAM_Instruction,
  output [2:0] Destination_Instruction,
  output Source_Enable,
  output [2:0] Source_Instruction
);

  wire d_ff_1_qn, d_ff_2_qn;

  D_Flip_Flop d_ff_1 (.clk(CLK), .D(Enable), .Q(Destination_Enable), .Qn(d_ff_1_qn));  // open: preset, en, reset
  D_Flip_Flop d_ff_2 (.clk(CLK), .D(Destination_Enable), .Q(RAM_Enable), .Qn(d_ff_2_qn));  // open: preset, en, reset
  and and_1 (Instruction_Running, d_ff_2_qn, d_ff_1_qn);

  assign Destination_Instruction = 3'b000;
  assign RAM_Instruction = {2'b00, RAM_Enable, {5{1'b0}}};
  assign Source_Enable = Destination_Enable;
  assign Source_Instruction = {{2{Destination_Enable}}, 1'b0};
endmodule

module Command_Unit_mov_reg__reg (
  input  CLK,
  input  Enable,
  output Instruction_Running,
  output RAM_Enable,
  output Destination_Enable,
  output [7:0] RAM_Instruction,
  output [2:0] Destination_Instruction,
  output Source_Enable,
  output [2:0] Source_Instruction
);

  wire d_ff_1_qn, d_ff_2_qn, d_ff_3_qn;

  D_Flip_Flop d_ff_1 (.clk(CLK), .D(Enable), .Q(RAM_Instruction[6]), .Qn(d_ff_1_qn));  // open: preset, en, reset
  D_Flip_Flop d_ff_2 (
    .clk(CLK), .D(RAM_Instruction[6]), .Q(Destination_Enable), .Qn(d_ff_2_qn));  // open: preset, en, reset
  D_Flip_Flop d_ff_3 (
    .clk(CLK), .D(Destination_Enable), .Q(RAM_Instruction[5]), .Qn(d_ff_3_qn));  // open: preset, en, reset
  and and_1 (Instruction_Running, d_ff_3_qn, d_ff_2_qn, d_ff_1_qn);
  or or_1 (RAM_Enable, RAM_Instruction[5], Destination_Enable, RAM_Instruction[6]);

  assign Destination_Instruction = 3'b000;
  assign {RAM_Instruction[7], RAM_Instruction[4:0]} = {{3{Destination_Enable}}, 3'b000};
  assign Source_Enable = RAM_Instruction[6];
  assign Source_Instruction = {{2{RAM_Instruction[6]}}, 1'b0};
endmodule

module Command_Unit_mov__reg__reg (
  input  CLK,
  input  Enable,
  output Instruction_Running,
  output RAM_Enable,
  output Destination_Enable,
  output [7:0] RAM_Instruction,
  output [2:0] Destination_Instruction,
  output Source_Enable,
  output [2:0] Source_Instruction
);

  wire d_ff_1_qn, d_ff_2_qn, d_ff_3_qn;

  D_Flip_Flop d_ff_1 (.clk(CLK), .D(Enable), .Q(Destination_Enable), .Qn(d_ff_1_qn));  // open: preset, en, reset
  D_Flip_Flop d_ff_2 (
    .clk(CLK), .D(Destination_Enable), .Q(RAM_Instruction[7]), .Qn(d_ff_2_qn));  // open: preset, en, reset
  D_Flip_Flop d_ff_3 (
    .clk(CLK), .D(RAM_Instruction[7]), .Q(RAM_Instruction[5]), .Qn(d_ff_3_qn));  // open: preset, en, reset
  and and_1 (Instruction_Running, d_ff_3_qn, d_ff_2_qn, d_ff_1_qn);
  or or_1 (RAM_Enable, RAM_Instruction[5], RAM_Instruction[7], Destination_Enable);

  assign Destination_Instruction = {{2{Destination_Enable}}, 1'b0};
  assign {RAM_Instruction[6], RAM_Instruction[4:0]} = {Destination_Enable, 2'b00, RAM_Instruction[7], 2'b00};
  assign Source_Enable = RAM_Instruction[7];
  assign Source_Instruction = {{2{RAM_Instruction[7]}}, 1'b0};
endmodule

module Command_Unit_add_reg_reg (
  input  CLK,
  input  Enable,
  output Instruction_Running,
  output RAM_Enable,
  output Destination_Enable,
  output [7:0] RAM_Instruction,
  output [2:0] Destination_Instruction,
  output Source_Enable,
  output [2:0] Source_Instruction,
  output Math_Enable,
  output [3:0] Math_Instruction
);

  wire d_ff_1_qn, d_ff_2_qn, d_ff_3_qn, d_ff_4_qn;

  D_Flip_Flop d_ff_1 (
    .clk(CLK), .D(Enable), .Q(Destination_Instruction[2]), .Qn(d_ff_1_qn));  // open: preset, en, reset
  or or_1 (Destination_Enable, Math_Instruction[2], Destination_Instruction[2]);
  D_Flip_Flop d_ff_2 (
    .clk(CLK), .D(Destination_Instruction[2]), .Q(Math_Instruction[0]), .Qn(d_ff_2_qn));  // open: preset, en, reset
  D_Flip_Flop d_ff_3 (
    .clk(CLK), .D(Math_Instruction[0]), .Q(Math_Instruction[2]), .Qn(d_ff_3_qn));  // open: preset, en, reset
  D_Flip_Flop d_ff_4 (.clk(CLK), .D(Math_Instruction[2]), .Q(RAM_Enable), .Qn(d_ff_4_qn));  // open: preset, en, reset
  or or_2 (Math_Instruction[3], Math_Instruction[0], Destination_Instruction[2]);
  and and_1 (Instruction_Running, d_ff_4_qn, d_ff_3_qn, d_ff_2_qn, d_ff_1_qn);
  or or_3 (Math_Enable, Destination_Instruction[2], Math_Instruction[0], Math_Instruction[2]);

  assign Destination_Instruction[1:0] = {Destination_Instruction[2], 1'b0};
  assign Math_Instruction[1] = 1'b0;
  assign RAM_Instruction = {2'b00, RAM_Enable, {5{1'b0}}};
  assign Source_Enable = Math_Instruction[0];
  assign Source_Instruction = {{2{Math_Instruction[0]}}, 1'b0};
endmodule

module Command_Unit_sub_reg_reg (
  input  CLK,
  input  Enable,
  output Instruction_Running,
  output RAM_Enable,
  output Destination_Enable,
  output [7:0] RAM_Instruction,
  output [2:0] Destination_Instruction,
  output Source_Enable,
  output [2:0] Source_Instruction,
  output Math_Enable,
  output [3:0] Math_Instruction
);

  wire d_ff_1_qn, d_ff_2_qn, d_ff_3_qn, d_ff_4_qn;

  D_Flip_Flop d_ff_1 (
    .clk(CLK), .D(Enable), .Q(Destination_Instruction[2]), .Qn(d_ff_1_qn));  // open: preset, en, reset
  or or_1 (Destination_Enable, Math_Instruction[2], Destination_Instruction[2]);
  D_Flip_Flop d_ff_2 (
    .clk(CLK), .D(Destination_Instruction[2]), .Q(Math_Instruction[0]), .Qn(d_ff_2_qn));  // open: preset, en, reset
  D_Flip_Flop d_ff_3 (
    .clk(CLK), .D(Math_Instruction[0]), .Q(Math_Instruction[2]), .Qn(d_ff_3_qn));  // open: preset, en, reset
  D_Flip_Flop d_ff_4 (.clk(CLK), .D(Math_Instruction[2]), .Q(RAM_Enable), .Qn(d_ff_4_qn));  // open: preset, en, reset
  or or_2 (Math_Instruction[3], Math_Instruction[0], Destination_Instruction[2]);
  and and_1 (Instruction_Running, d_ff_4_qn, d_ff_3_qn, d_ff_2_qn, d_ff_1_qn);
  or or_3 (Math_Enable, Destination_Instruction[2], Math_Instruction[0], Math_Instruction[2]);

  assign Destination_Instruction[1:0] = {Destination_Instruction[2], 1'b0};
  assign Math_Instruction[1] = Math_Instruction[2];
  assign RAM_Instruction = {2'b00, RAM_Enable, {5{1'b0}}};
  assign Source_Enable = Math_Instruction[0];
  assign Source_Instruction = {{2{Math_Instruction[0]}}, 1'b0};
endmodule

module Command_Unit_cmp_reg_reg (
  input  CLK,
  input  Enable,
  output Instruction_Running,
  output RAM_Enable,
  output Destination_Enable,
  output [7:0] RAM_Instruction,
  output [2:0] Destination_Instruction,
  output Source_Enable,
  output [2:0] Source_Instruction,
  output Compare_Enable,
  output Compare_Instruction
);

  wire d_ff_1_qn, d_ff_2_qn, d_ff_3_qn;

  D_Flip_Flop d_ff_1 (.clk(CLK), .D(Enable), .Q(Destination_Enable), .Qn(d_ff_1_qn));  // open: preset, en, reset
  D_Flip_Flop d_ff_2 (
    .clk(CLK), .D(Destination_Enable), .Q(Compare_Instruction), .Qn(d_ff_2_qn));  // open: preset, en, reset
  D_Flip_Flop d_ff_3 (.clk(CLK), .D(Compare_Instruction), .Q(RAM_Enable), .Qn(d_ff_3_qn));  // open: preset, en, reset
  and and_1 (Instruction_Running, d_ff_3_qn, d_ff_2_qn, d_ff_1_qn);
  or or_1 (Compare_Enable, Compare_Instruction, Destination_Enable);

  assign Destination_Instruction = {{2{Destination_Enable}}, 1'b0};
  assign RAM_Instruction = {2'b00, RAM_Enable, {5{1'b0}}};
  assign Source_Enable = Compare_Instruction;
  assign Source_Instruction = {{2{Compare_Instruction}}, 1'b0};
endmodule

module BUS_Command_Unit_V4 (
  input  CLK,
  input  [15:0] Data_In,
  output ax_enable_instruction,
  output [2:0] ax_instruction,
  output bx_enable_instruction,
  output [2:0] bx_instruction,
  output cx_enable_instruction,
  output [2:0] cx_instruction,
  output RAM0_Instruction_Enable,
  output [7:0] RAM0_Instruction,
  output dx_enable_instruction,
  output [2:0] dx_instruction
);

  wire and_1_out, and_2_out, and_3_out, and_4_out, and_5_out, and_6_out, and_7_out, and_8_out, and_9_out,
       and_10_out, and_11_out, and_12_out, and_13_out, and_14_out, and_15_out, and_16_out, and_17_out,
       and_18_out, and_19_out, and_20_out, and_21_out, and_22_out, and_23_out, and_24_out, and_25_out,
       command_unit_mov_reg_reg_1_destination_enable, command_unit_mov_reg_reg_1_instruction_running,
       command_unit_mov_reg_reg_1_ram_enable, command_unit_mov_reg_reg_1_source_enable,
       command_unit_mov_reg_reg_2_destination_enable, command_unit_mov_reg_reg_2_instruction_running,
       command_unit_mov_reg_reg_2_ram_enable, command_unit_mov_reg_reg_2_source_enable,
       command_unit_mov_reg_reg_3_destination_enable, command_unit_mov_reg_reg_3_instruction_running,
       command_unit_mov_reg_reg_3_ram_enable, command_unit_mov_reg_reg_3_source_enable,
       command_unit_mov_reg_reg_4_destination_enable, command_unit_mov_reg_reg_4_instruction_running,
       command_unit_mov_reg_reg_4_ram_enable, command_unit_mov_reg_reg_4_source_enable,
       command_unit_mov_reg_reg_5_destination_enable, command_unit_mov_reg_reg_5_instruction_running,
       command_unit_mov_reg_reg_5_ram_enable, command_unit_mov_reg_reg_5_source_enable,
       command_unit_mov_reg_reg_6_destination_enable, command_unit_mov_reg_reg_6_instruction_running,
       command_unit_mov_reg_reg_6_ram_enable, command_unit_mov_reg_reg_6_source_enable,
       command_unit_mov_reg_reg_7_destination_enable, command_unit_mov_reg_reg_7_instruction_running,
       command_unit_mov_reg_reg_7_ram_enable, command_unit_mov_reg_reg_7_source_enable,
       command_unit_mov_reg_reg_8_destination_enable, command_unit_mov_reg_reg_8_instruction_running,
       command_unit_mov_reg_reg_8_ram_enable, command_unit_mov_reg_reg_8_source_enable,
       command_unit_mov_reg_reg_9_destination_enable, command_unit_mov_reg_reg_9_instruction_running,
       command_unit_mov_reg_reg_9_ram_enable, command_unit_mov_reg_reg_9_source_enable,
       command_unit_mov_reg_reg_10_destination_enable, command_unit_mov_reg_reg_10_instruction_running,
       command_unit_mov_reg_reg_10_ram_enable, command_unit_mov_reg_reg_10_source_enable,
       command_unit_mov_reg_reg_11_destination_enable, command_unit_mov_reg_reg_11_instruction_running,
       command_unit_mov_reg_reg_11_ram_enable, command_unit_mov_reg_reg_11_source_enable,
       command_unit_mov_reg_reg_12_destination_enable, command_unit_mov_reg_reg_12_instruction_running,
       command_unit_mov_reg_reg_12_ram_enable, command_unit_mov_reg_reg_12_source_enable,
       command_unit_mov_reg_reg_13_destination_enable, command_unit_mov_reg_reg_13_instruction_running,
       command_unit_mov_reg_reg_13_ram_enable, command_unit_mov_reg_reg_13_source_enable,
       command_unit_mov_reg_reg_14_destination_enable, command_unit_mov_reg_reg_14_instruction_running,
       command_unit_mov_reg_reg_14_ram_enable, command_unit_mov_reg_reg_14_source_enable,
       command_unit_mov_reg_reg_15_destination_enable, command_unit_mov_reg_reg_15_instruction_running,
       command_unit_mov_reg_reg_15_ram_enable, command_unit_mov_reg_reg_15_source_enable,
       command_unit_mov_reg_reg_16_destination_enable, command_unit_mov_reg_reg_16_instruction_running,
       command_unit_mov_reg_reg_16_ram_enable, command_unit_mov_reg_reg_16_source_enable,
       command_unit_mov_reg_reg_17_destination_enable, command_unit_mov_reg_reg_17_instruction_running,
       command_unit_mov_reg_reg_17_ram_enable, command_unit_mov_reg_reg_17_source_enable,
       command_unit_mov_reg_reg_18_destination_enable, command_unit_mov_reg_reg_18_instruction_running,
       command_unit_mov_reg_reg_18_ram_enable, command_unit_mov_reg_reg_18_source_enable,
       command_unit_mov_reg_reg_19_destination_enable, command_unit_mov_reg_reg_19_instruction_running,
       command_unit_mov_reg_reg_19_ram_enable, command_unit_mov_reg_reg_19_source_enable,
       command_unit_mov_reg_reg_20_destination_enable, command_unit_mov_reg_reg_20_instruction_running,
       command_unit_mov_reg_reg_20_ram_enable, command_unit_mov_reg_reg_20_source_enable,
       command_unit_mov_reg_reg_21_destination_enable, command_unit_mov_reg_reg_21_instruction_running,
       command_unit_mov_reg_reg_21_ram_enable, command_unit_mov_reg_reg_21_source_enable,
       command_unit_mov_reg_reg_22_destination_enable, command_unit_mov_reg_reg_22_instruction_running,
       command_unit_mov_reg_reg_22_ram_enable, command_unit_mov_reg_reg_22_source_enable,
       command_unit_mov_reg_value16_1_instruction_running, command_unit_mov_reg_value16_1_ram_enable,
       command_unit_mov_reg_value16_1_register_enable, command_unit_mov_reg_value16_2_instruction_running,
       command_unit_mov_reg_value16_2_ram_enable, command_unit_mov_reg_value16_2_register_enable,
       command_unit_mov_reg_value16_3_instruction_running, command_unit_mov_reg_value16_3_ram_enable,
       command_unit_mov_reg_value16_3_register_enable, command_unit_mov_reg_value16_4_instruction_running,
       command_unit_mov_reg_value16_4_ram_enable, command_unit_mov_reg_value16_4_register_enable,
       mov_ax__ax_out, mov_ax__bx_out, mov_ax__cx_out, mov_ax__dx_out, mov_ax_bx_out, mov_ax_cx_out,
       mov_ax_dx_out, mov_ax_value16_out, mov_bx__ax_out, mov_bx__bx_out, mov_bx__cx_out, mov_bx__dx_out,
       mov_bx_ax_out, mov_bx_cx_out, mov_bx_dx_out, mov_bx_value16_out, mov_cx__ax_out, mov_cx__bx_out,
       mov_cx_ax_out, mov_cx_bx_out, mov_cx_dx_out, mov_cx_value16_out, mov_dx_ax_out, mov_dx_bx_out,
       mov_dx_cx_out, mov_dx_value16_out, or_10_out, or_12_out, or_15_out, or_17_out, or_18_out, or_19_out,
       or_22_out, or_24_out, or_36_out, or_38_out, or_41_out, or_42_out, or_44_out, or_46_out, or_48_out,
       or_52_out, or_54_out, or_55_out, or_58_out, or_61_out, or_63_out, or_64_out, or_66_out, or_68_out,
       or_70_out, or_74_out, or_76_out, or_77_out, or_78_out, or_80_out, or_81_out, or_82_out, or_83_out,
       or_84_out, or_85_out, or_86_out, or_87_out, or_88_out, or_89_out, or_90_out, or_91_out, or_92_out,
       or_93_out, or_94_out, or_95_out, or_96_out, or_97_out, or_98_out, or_99_out, or_100_out, or_101_out,
       or_102_out, or_103_out, or_104_out, or_105_out, or_106_out, or_107_out, or_108_out, or_109_out,
       or_110_out, or_111_out, or_112_out, or_113_out, or_114_out, or_115_out, or_117_out, or_119_out,
       or_143_out;
  wire [2:0] command_unit_mov_reg_reg_1_destination_instruction,
       command_unit_mov_reg_reg_1_source_instruction, command_unit_mov_reg_reg_2_destination_instruction,
       command_unit_mov_reg_reg_2_source_instruction, command_unit_mov_reg_reg_3_destination_instruction,
       command_unit_mov_reg_reg_3_source_instruction, command_unit_mov_reg_reg_4_destination_instruction,
       command_unit_mov_reg_reg_4_source_instruction, command_unit_mov_reg_reg_5_destination_instruction,
       command_unit_mov_reg_reg_5_source_instruction, command_unit_mov_reg_reg_6_destination_instruction,
       command_unit_mov_reg_reg_6_source_instruction, command_unit_mov_reg_reg_7_destination_instruction,
       command_unit_mov_reg_reg_7_source_instruction, command_unit_mov_reg_reg_8_destination_instruction,
       command_unit_mov_reg_reg_8_source_instruction, command_unit_mov_reg_reg_9_destination_instruction,
       command_unit_mov_reg_reg_9_source_instruction, command_unit_mov_reg_reg_10_destination_instruction,
       command_unit_mov_reg_reg_10_source_instruction, command_unit_mov_reg_reg_11_destination_instruction,
       command_unit_mov_reg_reg_11_source_instruction, command_unit_mov_reg_reg_12_destination_instruction,
       command_unit_mov_reg_reg_12_source_instruction, command_unit_mov_reg_reg_13_destination_instruction,
       command_unit_mov_reg_reg_13_source_instruction, command_unit_mov_reg_reg_14_destination_instruction,
       command_unit_mov_reg_reg_14_source_instruction, command_unit_mov_reg_reg_15_destination_instruction,
       command_unit_mov_reg_reg_15_source_instruction, command_unit_mov_reg_reg_16_destination_instruction,
       command_unit_mov_reg_reg_16_source_instruction, command_unit_mov_reg_reg_17_destination_instruction,
       command_unit_mov_reg_reg_17_source_instruction, command_unit_mov_reg_reg_18_destination_instruction,
       command_unit_mov_reg_reg_18_source_instruction, command_unit_mov_reg_reg_19_destination_instruction,
       command_unit_mov_reg_reg_19_source_instruction, command_unit_mov_reg_reg_20_destination_instruction,
       command_unit_mov_reg_reg_20_source_instruction, command_unit_mov_reg_reg_21_destination_instruction,
       command_unit_mov_reg_reg_21_source_instruction, command_unit_mov_reg_reg_22_destination_instruction,
       command_unit_mov_reg_reg_22_source_instruction, command_unit_mov_reg_value16_1_register_instruction,
       command_unit_mov_reg_value16_2_register_instruction,
       command_unit_mov_reg_value16_3_register_instruction,
       command_unit_mov_reg_value16_4_register_instruction, or_1_out, or_2_out, or_3_out, or_4_out, or_5_out,
       or_6_out, or_7_out, or_8_out, or_9_out, or_11_out, or_13_out, or_14_out, or_16_out, or_20_out,
       or_21_out, or_23_out, or_25_out, or_26_out, or_35_out, or_37_out, or_39_out, or_40_out, or_43_out,
       or_45_out, or_47_out, or_49_out, or_50_out, or_51_out, or_53_out, or_56_out, or_57_out, or_59_out,
       or_60_out, or_62_out, or_65_out, or_67_out, or_69_out, or_71_out, or_72_out, or_73_out, or_75_out,
       or_79_out;
  wire [7:0] command_unit_mov_reg_reg_1_ram_instruction, command_unit_mov_reg_reg_2_ram_instruction,
       command_unit_mov_reg_reg_3_ram_instruction, command_unit_mov_reg_reg_4_ram_instruction,
       command_unit_mov_reg_reg_5_ram_instruction, command_unit_mov_reg_reg_6_ram_instruction,
       command_unit_mov_reg_reg_7_ram_instruction, command_unit_mov_reg_reg_8_ram_instruction,
       command_unit_mov_reg_reg_9_ram_instruction, command_unit_mov_reg_reg_10_ram_instruction,
       command_unit_mov_reg_reg_11_ram_instruction, command_unit_mov_reg_reg_12_ram_instruction,
       command_unit_mov_reg_reg_13_ram_instruction, command_unit_mov_reg_reg_14_ram_instruction,
       command_unit_mov_reg_reg_15_ram_instruction, command_unit_mov_reg_reg_16_ram_instruction,
       command_unit_mov_reg_reg_17_ram_instruction, command_unit_mov_reg_reg_18_ram_instruction,
       command_unit_mov_reg_reg_19_ram_instruction, command_unit_mov_reg_reg_20_ram_instruction,
       command_unit_mov_reg_reg_21_ram_instruction, command_unit_mov_reg_reg_22_ram_instruction,
       command_unit_mov_reg_value16_1_ram_instruction, command_unit_mov_reg_value16_2_ram_instruction,
       command_unit_mov_reg_value16_3_ram_instruction, command_unit_mov_reg_value16_4_ram_instruction,
       or_116_out, or_118_out, or_120_out, or_121_out, or_122_out, or_123_out, or_124_out, or_125_out,
       or_126_out, or_127_out, or_128_out, or_129_out, or_130_out, or_131_out, or_132_out, or_133_out,
       or_134_out, or_135_out, or_136_out, or_137_out, or_138_out, or_139_out, or_140_out, or_141_out,
       or_142_out, or_144_out;
  wire [15:0] and_27_out;
  wire [15:15] and_26_out;

  assign or_1_out = or_2_out | command_unit_mov_reg_reg_3_source_instruction;  // OR_Gate or_1, 3 bits wide
  assign or_2_out = or_3_out | command_unit_mov_reg_reg_6_source_instruction;  // OR_Gate or_2, 3 bits wide
  assign or_3_out = or_4_out | command_unit_mov_reg_reg_9_source_instruction;  // OR_Gate or_3, 3 bits wide
  assign or_4_out = or_5_out | command_unit_mov_reg_reg_10_destination_instruction;  // OR_Gate or_4, 3 bits wide
  assign or_5_out = or_6_out | command_unit_mov_reg_reg_11_destination_instruction;  // OR_Gate or_5, 3 bits wide
  assign or_6_out = or_7_out | command_unit_mov_reg_reg_12_destination_instruction;  // OR_Gate or_6, 3 bits wide
  assign or_7_out = or_8_out | command_unit_mov_reg_reg_16_source_instruction;  // OR_Gate or_7, 3 bits wide
  assign or_8_out = command_unit_mov_reg_reg_20_source_instruction;  // OR_Gate or_8, 3 bits wide OR_Gate
  assign or_9_out = or_11_out | command_unit_mov_reg_reg_2_source_instruction;  // OR_Gate or_9, 3 bits wide
  or or_10 (or_10_out, or_12_out, command_unit_mov_reg_reg_3_source_enable);
  assign or_11_out = or_13_out | command_unit_mov_reg_reg_5_source_instruction;  // OR_Gate or_11, 3 bits wide
  or or_12 (or_12_out, or_15_out, command_unit_mov_reg_reg_6_source_enable);
  assign or_13_out = or_14_out | command_unit_mov_reg_reg_7_destination_instruction;  // OR_Gate or_13, 3 bits wide
  assign or_14_out = or_16_out | command_unit_mov_reg_reg_8_destination_instruction;  // OR_Gate or_14, 3 bits wide
  or or_15 (or_15_out, or_17_out, command_unit_mov_reg_reg_9_source_enable);
  assign or_16_out = or_20_out | command_unit_mov_reg_reg_9_destination_instruction;  // OR_Gate or_16, 3 bits wide
  or or_17 (or_17_out, or_18_out, command_unit_mov_reg_reg_10_destination_enable);
  or or_18 (or_18_out, or_19_out, command_unit_mov_reg_reg_11_destination_enable);
  or or_19 (or_19_out, or_22_out, command_unit_mov_reg_reg_12_destination_enable);
  assign or_20_out = or_21_out | command_unit_mov_reg_reg_12_source_instruction;  // OR_Gate or_20, 3 bits wide
  assign or_21_out = or_23_out | command_unit_mov_reg_reg_15_source_instruction;  // OR_Gate or_21, 3 bits wide
  or or_22 (or_22_out, or_24_out, command_unit_mov_reg_reg_16_source_enable);
  assign or_23_out = or_25_out | command_unit_mov_reg_reg_19_source_instruction;  // OR_Gate or_23, 3 bits wide
  buf or_24 (or_24_out, command_unit_mov_reg_reg_20_source_enable);  // OR_Gate
  assign or_25_out = or_26_out | command_unit_mov_reg_reg_21_destination_instruction;  // OR_Gate or_25, 3 bits wide
  assign or_26_out = command_unit_mov_reg_reg_22_destination_instruction;  // OR_Gate or_26, 3 bits wide OR_Gate
  or or_27 (ax_enable_instruction, command_unit_mov_reg_value16_4_register_enable, or_81_out);
  assign ax_instruction = command_unit_mov_reg_value16_4_register_instruction | or_57_out;  // OR_Gate or_28, 3 bits wide
  or or_29 (bx_enable_instruction, command_unit_mov_reg_value16_1_register_enable, or_58_out);
  assign bx_instruction = command_unit_mov_reg_value16_1_register_instruction | or_35_out;  // OR_Gate or_30, 3 bits wide
  or or_31 (cx_enable_instruction, command_unit_mov_reg_value16_2_register_enable, or_36_out);
  assign cx_instruction = command_unit_mov_reg_value16_2_register_instruction | or_9_out;  // OR_Gate or_32, 3 bits wide
  or or_33 (dx_enable_instruction, command_unit_mov_reg_value16_3_register_enable, or_10_out);
  assign dx_instruction = command_unit_mov_reg_value16_3_register_instruction | or_1_out;  // OR_Gate or_34, 3 bits wide
  assign or_35_out = or_37_out | command_unit_mov_reg_reg_1_source_instruction;  // OR_Gate or_35, 3 bits wide
  or or_36 (or_36_out, or_38_out, command_unit_mov_reg_reg_2_source_enable);
  assign or_37_out = or_39_out | command_unit_mov_reg_reg_4_destination_instruction;  // OR_Gate or_37, 3 bits wide
  or or_38 (or_38_out, or_41_out, command_unit_mov_reg_reg_5_source_enable);
  assign or_39_out = or_40_out | command_unit_mov_reg_reg_5_destination_instruction;  // OR_Gate or_39, 3 bits wide
  assign or_40_out = or_43_out | command_unit_mov_reg_reg_6_destination_instruction;  // OR_Gate or_40, 3 bits wide
  or or_41 (or_41_out, or_42_out, command_unit_mov_reg_reg_7_destination_enable);
  or or_42 (or_42_out, or_44_out, command_unit_mov_reg_reg_8_destination_enable);
  assign or_43_out = or_45_out | command_unit_mov_reg_reg_8_source_instruction;  // OR_Gate or_43, 3 bits wide
  or or_44 (or_44_out, or_46_out, command_unit_mov_reg_reg_9_destination_enable);
  assign or_45_out = or_47_out | command_unit_mov_reg_reg_11_source_instruction;  // OR_Gate or_45, 3 bits wide
  or or_46 (or_46_out, or_48_out, command_unit_mov_reg_reg_12_source_enable);
  assign or_47_out = or_49_out | command_unit_mov_reg_reg_14_source_instruction;  // OR_Gate or_47, 3 bits wide
  or or_48 (or_48_out, or_52_out, command_unit_mov_reg_reg_15_source_enable);
  assign or_49_out = or_50_out | command_unit_mov_reg_reg_17_destination_instruction;  // OR_Gate or_49, 3 bits wide
  assign or_50_out = or_51_out | command_unit_mov_reg_reg_18_source_instruction | command_unit_mov_reg_reg_18_destination_instruction;  // OR_Gate or_50, 3 bits wide
  assign or_51_out = or_53_out | command_unit_mov_reg_reg_19_destination_instruction;  // OR_Gate or_51, 3 bits wide
  or or_52 (or_52_out, or_54_out, command_unit_mov_reg_reg_19_source_enable);
  assign or_53_out = or_56_out | command_unit_mov_reg_reg_20_destination_instruction;  // OR_Gate or_53, 3 bits wide
  or or_54 (or_54_out, or_55_out, command_unit_mov_reg_reg_21_destination_enable);
  buf or_55 (or_55_out, command_unit_mov_reg_reg_22_destination_enable);  // OR_Gate
  assign or_56_out = command_unit_mov_reg_reg_22_source_instruction;  // OR_Gate or_56, 3 bits wide OR_Gate
  assign or_57_out = or_59_out | command_unit_mov_reg_reg_1_destination_instruction;  // OR_Gate or_57, 3 bits wide
  or or_58 (or_58_out, or_61_out, command_unit_mov_reg_reg_1_source_enable);
  assign or_59_out = or_60_out | command_unit_mov_reg_reg_2_destination_instruction;  // OR_Gate or_59, 3 bits wide
  assign or_60_out = or_62_out | command_unit_mov_reg_reg_3_destination_instruction;  // OR_Gate or_60, 3 bits wide
  or or_61 (or_61_out, or_63_out, command_unit_mov_reg_reg_4_destination_enable);
  assign or_62_out = or_65_out | command_unit_mov_reg_reg_4_source_instruction;  // OR_Gate or_62, 3 bits wide
  or or_63 (or_63_out, or_64_out, command_unit_mov_reg_reg_5_destination_enable);
  or or_64 (or_64_out, or_66_out, command_unit_mov_reg_reg_6_destination_enable);
  assign or_65_out = or_67_out | command_unit_mov_reg_reg_7_source_instruction;  // OR_Gate or_65, 3 bits wide
  or or_66 (or_66_out, or_68_out, command_unit_mov_reg_reg_8_source_enable);
  assign or_67_out = or_69_out | command_unit_mov_reg_reg_10_source_instruction;  // OR_Gate or_67, 3 bits wide
  or or_68 (or_68_out, or_70_out, command_unit_mov_reg_reg_11_source_enable);
  assign or_69_out = or_71_out | command_unit_mov_reg_reg_13_source_instruction | command_unit_mov_reg_reg_13_destination_instruction;  // OR_Gate or_69, 3 bits wide
  or or_70 (or_70_out, or_74_out, command_unit_mov_reg_reg_14_source_enable);
  assign or_71_out = or_72_out | command_unit_mov_reg_reg_14_destination_instruction;  // OR_Gate or_71, 3 bits wide
  assign or_72_out = or_73_out | command_unit_mov_reg_reg_15_destination_instruction;  // OR_Gate or_72, 3 bits wide
  assign or_73_out = or_75_out | command_unit_mov_reg_reg_16_destination_instruction;  // OR_Gate or_73, 3 bits wide
  or or_74 (or_74_out, or_76_out, command_unit_mov_reg_reg_17_destination_enable);
  assign or_75_out = or_79_out | command_unit_mov_reg_reg_17_source_instruction;  // OR_Gate or_75, 3 bits wide
  or or_76 (or_76_out, or_77_out, command_unit_mov_reg_reg_18_source_enable, command_unit_mov_reg_reg_18_destination_enable);
  or or_77 (or_77_out, or_78_out, command_unit_mov_reg_reg_19_destination_enable);
  or or_78 (or_78_out, or_80_out, command_unit_mov_reg_reg_20_destination_enable);
  assign or_79_out = command_unit_mov_reg_reg_21_source_instruction;  // OR_Gate or_79, 3 bits wide OR_Gate
  buf or_80 (or_80_out, command_unit_mov_reg_reg_22_source_enable);  // OR_Gate
  or or_81 (or_81_out, or_82_out, command_unit_mov_reg_reg_1_destination_enable);
  or or_82 (or_82_out, or_83_out, command_unit_mov_reg_reg_2_destination_enable);
  or or_83 (or_83_out, or_84_out, command_unit_mov_reg_reg_3_destination_enable);
  or or_84 (or_84_out, or_85_out, command_unit_mov_reg_reg_4_source_enable);
  or or_85 (or_85_out, or_86_out, command_unit_mov_reg_reg_7_source_enable);
  or or_86 (or_86_out, or_87_out, command_unit_mov_reg_reg_10_source_enable);
  or or_87 (or_87_out, or_88_out, command_unit_mov_reg_reg_13_source_enable, command_unit_mov_reg_reg_13_destination_enable);
  or or_88 (or_88_out, or_89_out, command_unit_mov_reg_reg_14_destination_enable);
  or or_89 (or_89_out, or_90_out, command_unit_mov_reg_reg_15_destination_enable);
  or or_90 (or_90_out, or_91_out, command_unit_mov_reg_reg_16_destination_enable);
  or or_91 (or_91_out, or_92_out, command_unit_mov_reg_reg_17_source_enable);
  buf or_92 (or_92_out, command_unit_mov_reg_reg_21_source_enable);  // OR_Gate
  Command_Unit_mov_reg_value16 command_unit_mov_reg_value16_1 (
    .CLK(CLK), .Enable(mov_bx_value16_out), .Register_Enable(command_unit_mov_reg_value16_1_register_enable),
    .Register_Instruction(command_unit_mov_reg_value16_1_register_instruction),
    .Instruction_Running(command_unit_mov_reg_value16_1_instruction_running),
    .RAM_Enable(command_unit_mov_reg_value16_1_ram_enable),
    .RAM_Instruction(command_unit_mov_reg_value16_1_ram_instruction));
  Command_Unit_mov_reg_value16 command_unit_mov_reg_value16_2 (
    .CLK(CLK), .Enable(mov_cx_value16_out), .Register_Enable(command_unit_mov_reg_value16_2_register_enable),
    .Register_Instruction(command_unit_mov_reg_value16_2_register_instruction),
    .Instruction_Running(command_unit_mov_reg_value16_2_instruction_running),
    .RAM_Enable(command_unit_mov_reg_value16_2_ram_enable),
    .RAM_Instruction(command_unit_mov_reg_value16_2_ram_instruction));
  Command_Unit_mov_reg_value16 command_unit_mov_reg_value16_3 (
    .CLK(CLK), .Enable(mov_dx_value16_out), .Register_Enable(command_unit_mov_reg_value16_3_register_enable),
    .Register_Instruction(command_unit_mov_reg_value16_3_register_instruction),
    .Instruction_Running(command_unit_mov_reg_value16_3_instruction_running),
    .RAM_Enable(command_unit_mov_reg_value16_3_ram_enable),
    .RAM_Instruction(command_unit_mov_reg_value16_3_ram_instruction));
  Command_Unit_mov_reg_value16 command_unit_mov_reg_value16_4 (
    .CLK(CLK), .Enable(mov_ax_value16_out), .Register_Enable(command_unit_mov_reg_value16_4_register_enable),
    .Register_Instruction(command_unit_mov_reg_value16_4_register_instruction),
    .Instruction_Running(command_unit_mov_reg_value16_4_instruction_running),
    .RAM_Enable(command_unit_mov_reg_value16_4_ram_enable),
    .RAM_Instruction(command_unit_mov_reg_value16_4_ram_instruction));
  and and_1 (and_1_out, command_unit_mov_reg_value16_1_instruction_running, and_2_out);
  and and_2 (and_2_out, command_unit_mov_reg_value16_2_instruction_running, and_3_out);
  and and_3 (and_3_out, command_unit_mov_reg_value16_3_instruction_running, and_4_out);
  or or_93 (or_93_out, command_unit_mov_reg_reg_1_ram_enable, or_94_out);
  and and_4 (and_4_out, command_unit_mov_reg_reg_1_instruction_running, and_5_out);
  Command_Unit_mov_reg_reg command_unit_mov_reg_reg_1 (
    .CLK(CLK), .Enable(mov_ax_bx_out), .Destination_Enable(command_unit_mov_reg_reg_1_destination_enable),
    .Destination_Instruction(command_unit_mov_reg_reg_1_destination_instruction),
    .Source_Enable(command_unit_mov_reg_reg_1_source_enable),
    .Source_Instruction(command_unit_mov_reg_reg_1_source_instruction),
    .Instruction_Running(command_unit_mov_reg_reg_1_instruction_running),
    .RAM_Enable(command_unit_mov_reg_reg_1_ram_enable),
    .RAM_Instruction(command_unit_mov_reg_reg_1_ram_instruction));
  or or_94 (or_94_out, command_unit_mov_reg_reg_2_ram_enable, or_95_out);
  and and_5 (and_5_out, command_unit_mov_reg_reg_2_instruction_running, and_6_out);
  Command_Unit_mov_reg_reg command_unit_mov_reg_reg_2 (
    .CLK(CLK), .Enable(mov_ax_cx_out), .Destination_Enable(command_unit_mov_reg_reg_2_destination_enable),
    .Destination_Instruction(command_unit_mov_reg_reg_2_destination_instruction),
    .Source_Enable(command_unit_mov_reg_reg_2_source_enable),
    .Source_Instruction(command_unit_mov_reg_reg_2_source_instruction),
    .Instruction_Running(command_unit_mov_reg_reg_2_instruction_running),
    .RAM_Enable(command_unit_mov_reg_reg_2_ram_enable),
    .RAM_Instruction(command_unit_mov_reg_reg_2_ram_instruction));
  and and_6 (and_6_out, command_unit_mov_reg_reg_3_instruction_running, and_7_out);
  or or_95 (or_95_out, command_unit_mov_reg_reg_3_ram_enable, or_96_out);
  Command_Unit_mov_reg_reg command_unit_mov_reg_reg_3 (
    .CLK(CLK), .Enable(mov_ax_dx_out), .Destination_Enable(command_unit_mov_reg_reg_3_destination_enable),
    .Destination_Instruction(command_unit_mov_reg_reg_3_destination_instruction),
    .Source_Enable(command_unit_mov_reg_reg_3_source_enable),
    .Source_Instruction(command_unit_mov_reg_reg_3_source_instruction),
    .Instruction_Running(command_unit_mov_reg_reg_3_instruction_running),
    .RAM_Enable(command_unit_mov_reg_reg_3_ram_enable),
    .RAM_Instruction(command_unit_mov_reg_reg_3_ram_instruction));
  or or_96 (or_96_out, command_unit_mov_reg_reg_4_ram_enable, or_97_out);
  and and_7 (and_7_out, command_unit_mov_reg_reg_4_instruction_running, and_8_out);
  Command_Unit_mov_reg_reg command_unit_mov_reg_reg_4 (
    .CLK(CLK), .Enable(mov_bx_ax_out), .Destination_Enable(command_unit_mov_reg_reg_4_destination_enable),
    .Destination_Instruction(command_unit_mov_reg_reg_4_destination_instruction),
    .Source_Enable(command_unit_mov_reg_reg_4_source_enable),
    .Source_Instruction(command_unit_mov_reg_reg_4_source_instruction),
    .Instruction_Running(command_unit_mov_reg_reg_4_instruction_running),
    .RAM_Enable(command_unit_mov_reg_reg_4_ram_enable),
    .RAM_Instruction(command_unit_mov_reg_reg_4_ram_instruction));
  or or_97 (or_97_out, command_unit_mov_reg_reg_5_ram_enable, or_98_out);
  and and_8 (and_8_out, command_unit_mov_reg_reg_5_instruction_running, and_9_out);
  Command_Unit_mov_reg_reg command_unit_mov_reg_reg_5 (
    .CLK(CLK), .Enable(mov_bx_cx_out), .Destination_Enable(command_unit_mov_reg_reg_5_destination_enable),
    .Destination_Instruction(command_unit_mov_reg_reg_5_destination_instruction),
    .Source_Enable(command_unit_mov_reg_reg_5_source_enable),
    .Source_Instruction(command_unit_mov_reg_reg_5_source_instruction),
    .Instruction_Running(command_unit_mov_reg_reg_5_instruction_running),
    .RAM_Enable(command_unit_mov_reg_reg_5_ram_enable),
    .RAM_Instruction(command_unit_mov_reg_reg_5_ram_instruction));
  or or_98 (or_98_out, command_unit_mov_reg_reg_6_ram_enable, or_99_out);
  and and_9 (and_9_out, command_unit_mov_reg_reg_6_instruction_running, and_10_out);
  Command_Unit_mov_reg_reg command_unit_mov_reg_reg_6 (
    .CLK(CLK), .Enable(mov_bx_dx_out), .Destination_Enable(command_unit_mov_reg_reg_6_destination_enable),
    .Destination_Instruction(command_unit_mov_reg_reg_6_destination_instruction),
    .Source_Enable(command_unit_mov_reg_reg_6_source_enable),
    .Source_Instruction(command_unit_mov_reg_reg_6_source_instruction),
    .Instruction_Running(command_unit_mov_reg_reg_6_instruction_running),
    .RAM_Enable(command_unit_mov_reg_reg_6_ram_enable),
    .RAM_Instruction(command_unit_mov_reg_reg_6_ram_instruction));
  and and_10 (and_10_out, command_unit_mov_reg_reg_7_instruction_running, and_11_out);
  or or_99 (or_99_out, command_unit_mov_reg_reg_7_ram_enable, or_100_out);
  Command_Unit_mov_reg_reg command_unit_mov_reg_reg_7 (
    .CLK(CLK), .Enable(mov_cx_ax_out), .Destination_Enable(command_unit_mov_reg_reg_7_destination_enable),
    .Destination_Instruction(command_unit_mov_reg_reg_7_destination_instruction),
    .Source_Enable(command_unit_mov_reg_reg_7_source_enable),
    .Source_Instruction(command_unit_mov_reg_reg_7_source_instruction),
    .Instruction_Running(command_unit_mov_reg_reg_7_instruction_running),
    .RAM_Enable(command_unit_mov_reg_reg_7_ram_enable),
    .RAM_Instruction(command_unit_mov_reg_reg_7_ram_instruction));
  or or_100 (or_100_out, command_unit_mov_reg_reg_8_ram_enable, or_101_out);
  and and_11 (and_11_out, command_unit_mov_reg_reg_8_instruction_running, and_12_out);
  Command_Unit_mov_reg_reg command_unit_mov_reg_reg_8 (
    .CLK(CLK), .Enable(mov_cx_bx_out), .Destination_Enable(command_unit_mov_reg_reg_8_destination_enable),
    .Destination_Instruction(command_unit_mov_reg_reg_8_destination_instruction),
    .Source_Enable(command_unit_mov_reg_reg_8_source_enable),
    .Source_Instruction(command_unit_mov_reg_reg_8_source_instruction),
    .Instruction_Running(command_unit_mov_reg_reg_8_instruction_running),
    .RAM_Enable(command_unit_mov_reg_reg_8_ram_enable),
    .RAM_Instruction(command_unit_mov_reg_reg_8_ram_instruction));
  and and_12 (and_12_out, command_unit_mov_reg_reg_9_instruction_running, and_13_out);
  or or_101 (or_101_out, command_unit_mov_reg_reg_9_ram_enable, or_102_out);
  Command_Unit_mov_reg_reg command_unit_mov_reg_reg_9 (
    .CLK(CLK), .Enable(mov_cx_dx_out), .Destination_Enable(command_unit_mov_reg_reg_9_destination_enable),
    .Destination_Instruction(command_unit_mov_reg_reg_9_destination_instruction),
    .Source_Enable(command_unit_mov_reg_reg_9_source_enable),
    .Source_Instruction(command_unit_mov_reg_reg_9_source_instruction),
    .Instruction_Running(command_unit_mov_reg_reg_9_instruction_running),
    .RAM_Enable(command_unit_mov_reg_reg_9_ram_enable),
    .RAM_Instruction(command_unit_mov_reg_reg_9_ram_instruction));
  or or_102 (or_102_out, command_unit_mov_reg_reg_10_ram_enable, or_103_out);
  and and_13 (and_13_out, command_unit_mov_reg_reg_10_instruction_running, and_14_out);
  Command_Unit_mov_reg_reg command_unit_mov_reg_reg_10 (
    .CLK(CLK), .Enable(mov_dx_ax_out), .Destination_Enable(command_unit_mov_reg_reg_10_destination_enable),
    .Destination_Instruction(command_unit_mov_reg_reg_10_destination_instruction),
    .Source_Enable(command_unit_mov_reg_reg_10_source_enable),
    .Source_Instruction(command_unit_mov_reg_reg_10_source_instruction),
    .Instruction_Running(command_unit_mov_reg_reg_10_instruction_running),
    .RAM_Enable(command_unit_mov_reg_reg_10_ram_enable),
    .RAM_Instruction(command_unit_mov_reg_reg_10_ram_instruction));
  and and_14 (and_14_out, command_unit_mov_reg_reg_11_instruction_running, and_15_out);
  or or_103 (or_103_out, command_unit_mov_reg_reg_11_ram_enable, or_104_out);
  Command_Unit_mov_reg_reg command_unit_mov_reg_reg_11 (
    .CLK(CLK), .Enable(mov_dx_bx_out), .Destination_Enable(command_unit_mov_reg_reg_11_destination_enable),
    .Destination_Instruction(command_unit_mov_reg_reg_11_destination_instruction),
    .Source_Enable(command_unit_mov_reg_reg_11_source_enable),
    .Source_Instruction(command_unit_mov_reg_reg_11_source_instruction),
    .Instruction_Running(command_unit_mov_reg_reg_11_instruction_running),
    .RAM_Enable(command_unit_mov_reg_reg_11_ram_enable),
    .RAM_Instruction(command_unit_mov_reg_reg_11_ram_instruction));
  and and_15 (and_15_out, command_unit_mov_reg_reg_12_instruction_running, and_16_out);
  or or_104 (or_104_out, command_unit_mov_reg_reg_12_ram_enable, or_105_out);
  Command_Unit_mov_reg_reg command_unit_mov_reg_reg_12 (
    .CLK(CLK), .Enable(mov_dx_cx_out), .Destination_Enable(command_unit_mov_reg_reg_12_destination_enable),
    .Destination_Instruction(command_unit_mov_reg_reg_12_destination_instruction),
    .Source_Enable(command_unit_mov_reg_reg_12_source_enable),
    .Source_Instruction(command_unit_mov_reg_reg_12_source_instruction),
    .Instruction_Running(command_unit_mov_reg_reg_12_instruction_running),
    .RAM_Enable(command_unit_mov_reg_reg_12_ram_enable),
    .RAM_Instruction(command_unit_mov_reg_reg_12_ram_instruction));
  or or_105 (or_105_out, command_unit_mov_reg_reg_13_ram_enable, or_106_out);
  and and_16 (and_16_out, command_unit_mov_reg_reg_13_instruction_running, and_17_out);
  Command_Unit_mov_reg__reg command_unit_mov_reg_reg_13 (
    .CLK(CLK), .Enable(mov_ax__ax_out), .Destination_Enable(command_unit_mov_reg_reg_13_destination_enable),
    .Destination_Instruction(command_unit_mov_reg_reg_13_destination_instruction),
    .Source_Enable(command_unit_mov_reg_reg_13_source_enable),
    .Source_Instruction(command_unit_mov_reg_reg_13_source_instruction),
    .Instruction_Running(command_unit_mov_reg_reg_13_instruction_running),
    .RAM_Enable(command_unit_mov_reg_reg_13_ram_enable),
    .RAM_Instruction(command_unit_mov_reg_reg_13_ram_instruction));
  or or_106 (or_106_out, command_unit_mov_reg_reg_14_ram_enable, or_107_out);
  and and_17 (and_17_out, command_unit_mov_reg_reg_14_instruction_running, and_18_out);
  Command_Unit_mov_reg__reg command_unit_mov_reg_reg_14 (
    .CLK(CLK), .Enable(mov_ax__bx_out), .Destination_Enable(command_unit_mov_reg_reg_14_destination_enable),
    .Destination_Instruction(command_unit_mov_reg_reg_14_destination_instruction),
    .Source_Enable(command_unit_mov_reg_reg_14_source_enable),
    .Source_Instruction(command_unit_mov_reg_reg_14_source_instruction),
    .Instruction_Running(command_unit_mov_reg_reg_14_instruction_running),
    .RAM_Enable(command_unit_mov_reg_reg_14_ram_enable),
    .RAM_Instruction(command_unit_mov_reg_reg_14_ram_instruction));
  and and_18 (and_18_out, command_unit_mov_reg_reg_15_instruction_running, and_19_out);
  or or_107 (or_107_out, command_unit_mov_reg_reg_15_ram_enable, or_108_out);
  Command_Unit_mov_reg__reg command_unit_mov_reg_reg_15 (
    .CLK(CLK), .Enable(mov_ax__cx_out), .Destination_Enable(command_unit_mov_reg_reg_15_destination_enable),
    .Destination_Instruction(command_unit_mov_reg_reg_15_destination_instruction),
    .Source_Enable(command_unit_mov_reg_reg_15_source_enable),
    .Source_Instruction(command_unit_mov_reg_reg_15_source_instruction),
    .Instruction_Running(command_unit_mov_reg_reg_15_instruction_running),
    .RAM_Enable(command_unit_mov_reg_reg_15_ram_enable),
    .RAM_Instruction(command_unit_mov_reg_reg_15_ram_instruction));
  and and_19 (and_19_out, command_unit_mov_reg_reg_16_instruction_running, and_20_out);
  or or_108 (or_108_out, command_unit_mov_reg_reg_16_ram_enable, or_109_out);
  Command_Unit_mov_reg__reg command_unit_mov_reg_reg_16 (
    .CLK(CLK), .Enable(mov_ax__dx_out), .Destination_Enable(command_unit_mov_reg_reg_16_destination_enable),
    .Destination_Instruction(command_unit_mov_reg_reg_16_destination_instruction),
    .Source_Enable(command_unit_mov_reg_reg_16_source_enable),
    .Source_Instruction(command_unit_mov_reg_reg_16_source_instruction),
    .Instruction_Running(command_unit_mov_reg_reg_16_instruction_running),
    .RAM_Enable(command_unit_mov_reg_reg_16_ram_enable),
    .RAM_Instruction(command_unit_mov_reg_reg_16_ram_instruction));
  or or_109 (or_109_out, command_unit_mov_reg_reg_17_ram_enable, or_110_out);
  and and_20 (and_20_out, command_unit_mov_reg_reg_17_instruction_running, and_21_out);
  Command_Unit_mov_reg__reg command_unit_mov_reg_reg_17 (
    .CLK(CLK), .Enable(mov_bx__ax_out), .Destination_Enable(command_unit_mov_reg_reg_17_destination_enable),
    .Destination_Instruction(command_unit_mov_reg_reg_17_destination_instruction),
    .Source_Enable(command_unit_mov_reg_reg_17_source_enable),
    .Source_Instruction(command_unit_mov_reg_reg_17_source_instruction),
    .Instruction_Running(command_unit_mov_reg_reg_17_instruction_running),
    .RAM_Enable(command_unit_mov_reg_reg_17_ram_enable),
    .RAM_Instruction(command_unit_mov_reg_reg_17_ram_instruction));
  or or_110 (or_110_out, command_unit_mov_reg_reg_18_ram_enable, or_111_out);
  and and_21 (and_21_out, command_unit_mov_reg_reg_18_instruction_running, and_22_out);
  Command_Unit_mov_reg__reg command_unit_mov_reg_reg_18 (
    .CLK(CLK), .Enable(mov_bx__bx_out), .Destination_Enable(command_unit_mov_reg_reg_18_destination_enable),
    .Destination_Instruction(command_unit_mov_reg_reg_18_destination_instruction),
    .Source_Enable(command_unit_mov_reg_reg_18_source_enable),
    .Source_Instruction(command_unit_mov_reg_reg_18_source_instruction),
    .Instruction_Running(command_unit_mov_reg_reg_18_instruction_running),
    .RAM_Enable(command_unit_mov_reg_reg_18_ram_enable),
    .RAM_Instruction(command_unit_mov_reg_reg_18_ram_instruction));
  or or_111 (or_111_out, command_unit_mov_reg_reg_19_ram_enable, or_112_out);
  and and_22 (and_22_out, command_unit_mov_reg_reg_19_instruction_running, and_23_out);
  Command_Unit_mov_reg__reg command_unit_mov_reg_reg_19 (
    .CLK(CLK), .Enable(mov_bx__cx_out), .Destination_Enable(command_unit_mov_reg_reg_19_destination_enable),
    .Destination_Instruction(command_unit_mov_reg_reg_19_destination_instruction),
    .Source_Enable(command_unit_mov_reg_reg_19_source_enable),
    .Source_Instruction(command_unit_mov_reg_reg_19_source_instruction),
    .Instruction_Running(command_unit_mov_reg_reg_19_instruction_running),
    .RAM_Enable(command_unit_mov_reg_reg_19_ram_enable),
    .RAM_Instruction(command_unit_mov_reg_reg_19_ram_instruction));
  and and_23 (and_23_out, command_unit_mov_reg_reg_20_instruction_running, and_24_out);
  or or_112 (or_112_out, command_unit_mov_reg_reg_20_ram_enable, or_113_out);
  Command_Unit_mov_reg__reg command_unit_mov_reg_reg_20 (
    .CLK(CLK), .Enable(mov_bx__dx_out), .Destination_Enable(command_unit_mov_reg_reg_20_destination_enable),
    .Destination_Instruction(command_unit_mov_reg_reg_20_destination_instruction),
    .Source_Enable(command_unit_mov_reg_reg_20_source_enable),
    .Source_Instruction(command_unit_mov_reg_reg_20_source_instruction),
    .Instruction_Running(command_unit_mov_reg_reg_20_instruction_running),
    .RAM_Enable(command_unit_mov_reg_reg_20_ram_enable),
    .RAM_Instruction(command_unit_mov_reg_reg_20_ram_instruction));
  and and_24 (and_24_out, command_unit_mov_reg_reg_21_instruction_running, and_25_out);
  or or_113 (or_113_out, command_unit_mov_reg_reg_21_ram_enable, or_114_out);
  Command_Unit_mov_reg__reg command_unit_mov_reg_reg_21 (
    .CLK(CLK), .Enable(mov_cx__ax_out), .Destination_Enable(command_unit_mov_reg_reg_21_destination_enable),
    .Destination_Instruction(command_unit_mov_reg_reg_21_destination_instruction),
    .Source_Enable(command_unit_mov_reg_reg_21_source_enable),
    .Source_Instruction(command_unit_mov_reg_reg_21_source_instruction),
    .Instruction_Running(command_unit_mov_reg_reg_21_instruction_running),
    .RAM_Enable(command_unit_mov_reg_reg_21_ram_enable),
    .RAM_Instruction(command_unit_mov_reg_reg_21_ram_instruction));
  buf or_114 (or_114_out, command_unit_mov_reg_reg_22_ram_enable);  // OR_Gate
  buf and_25 (and_25_out, command_unit_mov_reg_reg_22_instruction_running);  // AND_Gate
  Command_Unit_mov_reg__reg command_unit_mov_reg_reg_22 (
    .CLK(CLK), .Enable(mov_cx__bx_out), .Destination_Enable(command_unit_mov_reg_reg_22_destination_enable),
    .Destination_Instruction(command_unit_mov_reg_reg_22_destination_instruction),
    .Source_Enable(command_unit_mov_reg_reg_22_source_enable),
    .Source_Instruction(command_unit_mov_reg_reg_22_source_instruction),
    .Instruction_Running(command_unit_mov_reg_reg_22_instruction_running),
    .RAM_Enable(command_unit_mov_reg_reg_22_ram_enable),
    .RAM_Instruction(command_unit_mov_reg_reg_22_ram_instruction));
  and and_26 (and_26_out[15], command_unit_mov_reg_value16_4_instruction_running, and_1_out);
  and mov_ax_value16 (mov_ax_value16_out, and_27_out[0], ~and_27_out[1], ~and_27_out[2], ~and_27_out[3], ~and_27_out[4], ~and_27_out[5], ~and_27_out[6], ~and_27_out[7], ~and_27_out[8], ~and_27_out[9], ~and_27_out[10], ~and_27_out[11], ~and_27_out[12], ~and_27_out[13], ~and_27_out[14], ~and_27_out[15]);  // AND_Gate
  and mov_bx_value16 (mov_bx_value16_out, ~and_27_out[0], and_27_out[1], ~and_27_out[2], ~and_27_out[3], ~and_27_out[4], ~and_27_out[5], ~and_27_out[6], ~and_27_out[7], ~and_27_out[8], ~and_27_out[9], ~and_27_out[10], ~and_27_out[11], ~and_27_out[12], ~and_27_out[13], ~and_27_out[14], ~and_27_out[15]);  // AND_Gate
  or or_115 (or_115_out, command_unit_mov_reg_value16_1_ram_enable, or_117_out);
  assign or_116_out = command_unit_mov_reg_value16_1_ram_instruction | or_118_out;  // OR_Gate or_116, 8 bits wide
  and mov_cx_value16 (mov_cx_value16_out, and_27_out[0], and_27_out[1], ~and_27_out[2], ~and_27_out[3], ~and_27_out[4], ~and_27_out[5], ~and_27_out[6], ~and_27_out[7], ~and_27_out[8], ~and_27_out[9], ~and_27_out[10], ~and_27_out[11], ~and_27_out[12], ~and_27_out[13], ~and_27_out[14], ~and_27_out[15]);  // AND_Gate
  or or_117 (or_117_out, command_unit_mov_reg_value16_2_ram_enable, or_119_out);
  assign or_118_out = command_unit_mov_reg_value16_2_ram_instruction | or_120_out;  // OR_Gate or_118, 8 bits wide
  and mov_dx_value16 (mov_dx_value16_out, ~and_27_out[0], ~and_27_out[1], and_27_out[2], ~and_27_out[3], ~and_27_out[4], ~and_27_out[5], ~and_27_out[6], ~and_27_out[7], ~and_27_out[8], ~and_27_out[9], ~and_27_out[10], ~and_27_out[11], ~and_27_out[12], ~and_27_out[13], ~and_27_out[14], ~and_27_out[15]);  // AND_Gate
  or or_119 (or_119_out, command_unit_mov_reg_value16_3_ram_enable, or_93_out);
  assign or_120_out = command_unit_mov_reg_value16_3_ram_instruction | or_121_out;  // OR_Gate or_120, 8 bits wide
  assign or_121_out = command_unit_mov_reg_reg_1_ram_instruction | or_122_out;  // OR_Gate or_121, 8 bits wide
  and mov_ax_bx (mov_ax_bx_out, and_27_out[0], ~and_27_out[1], and_27_out[2], ~and_27_out[3], ~and_27_out[4], ~and_27_out[5], ~and_27_out[6], ~and_27_out[7], ~and_27_out[8], ~and_27_out[9], ~and_27_out[10], ~and_27_out[11], ~and_27_out[12], ~and_27_out[13], ~and_27_out[14], ~and_27_out[15]);  // AND_Gate
  assign or_122_out = command_unit_mov_reg_reg_2_ram_instruction | or_123_out;  // OR_Gate or_122, 8 bits wide
  and mov_ax_cx (mov_ax_cx_out, ~and_27_out[0], and_27_out[1], and_27_out[2], ~and_27_out[3], ~and_27_out[4], ~and_27_out[5], ~and_27_out[6], ~and_27_out[7], ~and_27_out[8], ~and_27_out[9], ~and_27_out[10], ~and_27_out[11], ~and_27_out[12], ~and_27_out[13], ~and_27_out[14], ~and_27_out[15]);  // AND_Gate
  assign or_123_out = command_unit_mov_reg_reg_3_ram_instruction | or_124_out;  // OR_Gate or_123, 8 bits wide
  and mov_ax_dx (mov_ax_dx_out, and_27_out[0], and_27_out[1], and_27_out[2], ~and_27_out[3], ~and_27_out[4], ~and_27_out[5], ~and_27_out[6], ~and_27_out[7], ~and_27_out[8], ~and_27_out[9], ~and_27_out[10], ~and_27_out[11], ~and_27_out[12], ~and_27_out[13], ~and_27_out[14], ~and_27_out[15]);  // AND_Gate
  assign or_124_out = command_unit_mov_reg_reg_4_ram_instruction | or_125_out;  // OR_Gate or_124, 8 bits wide
  and mov_bx_ax (mov_bx_ax_out, ~and_27_out[0], ~and_27_out[1], ~and_27_out[2], and_27_out[3], ~and_27_out[4], ~and_27_out[5], ~and_27_out[6], ~and_27_out[7], ~and_27_out[8], ~and_27_out[9], ~and_27_out[10], ~and_27_out[11], ~and_27_out[12], ~and_27_out[13], ~and_27_out[14], ~and_27_out[15]);  // AND_Gate
  assign or_125_out = command_unit_mov_reg_reg_5_ram_instruction | or_126_out;  // OR_Gate or_125, 8 bits wide
  and mov_bx_cx (mov_bx_cx_out, and_27_out[0], ~and_27_out[1], ~and_27_out[2], and_27_out[3], ~and_27_out[4], ~and_27_out[5], ~and_27_out[6], ~and_27_out[7], ~and_27_out[8], ~and_27_out[9], ~and_27_out[10], ~and_27_out[11], ~and_27_out[12], ~and_27_out[13], ~and_27_out[14], ~and_27_out[15]);  // AND_Gate
  assign or_126_out = command_unit_mov_reg_reg_6_ram_instruction | or_127_out;  // OR_Gate or_126, 8 bits wide
  and mov_bx_dx (mov_bx_dx_out, ~and_27_out[0], and_27_out[1], ~and_27_out[2], and_27_out[3], ~and_27_out[4], ~and_27_out[5], ~and_27_out[6], ~and_27_out[7], ~and_27_out[8], ~and_27_out[9], ~and_27_out[10], ~and_27_out[11], ~and_27_out[12], ~and_27_out[13], ~and_27_out[14], ~and_27_out[15]);  // AND_Gate
  assign or_127_out = command_unit_mov_reg_reg_7_ram_instruction | or_128_out;  // OR_Gate or_127, 8 bits wide
  and mov_cx_ax (mov_cx_ax_out, and_27_out[0], and_27_out[1], ~and_27_out[2], and_27_out[3], ~and_27_out[4], ~and_27_out[5], ~and_27_out[6], ~and_27_out[7], ~and_27_out[8], ~and_27_out[9], ~and_27_out[10], ~and_27_out[11], ~and_27_out[12], ~and_27_out[13], ~and_27_out[14], ~and_27_out[15]);  // AND_Gate
  assign or_128_out = command_unit_mov_reg_reg_8_ram_instruction | or_129_out;  // OR_Gate or_128, 8 bits wide
  and mov_cx_bx (mov_cx_bx_out, ~and_27_out[0], ~and_27_out[1], and_27_out[2], and_27_out[3], ~and_27_out[4], ~and_27_out[5], ~and_27_out[6], ~and_27_out[7], ~and_27_out[8], ~and_27_out[9], ~and_27_out[10], ~and_27_out[11], ~and_27_out[12], ~and_27_out[13], ~and_27_out[14], ~and_27_out[15]);  // AND_Gate
  assign or_129_out = command_unit_mov_reg_reg_9_ram_instruction | or_130_out;  // OR_Gate or_129, 8 bits wide
  and mov_cx_dx (mov_cx_dx_out, and_27_out[0], ~and_27_out[1], and_27_out[2], and_27_out[3], ~and_27_out[4], ~and_27_out[5], ~and_27_out[6], ~and_27_out[7], ~and_27_out[8], ~and_27_out[9], ~and_27_out[10], ~and_27_out[11], ~and_27_out[12], ~and_27_out[13], ~and_27_out[14], ~and_27_out[15]);  // AND_Gate
  assign or_130_out = command_unit_mov_reg_reg_10_ram_instruction | or_131_out;  // OR_Gate or_130, 8 bits wide
  and mov_dx_ax (mov_dx_ax_out, ~and_27_out[0], and_27_out[1], and_27_out[2], and_27_out[3], ~and_27_out[4], ~and_27_out[5], ~and_27_out[6], ~and_27_out[7], ~and_27_out[8], ~and_27_out[9], ~and_27_out[10], ~and_27_out[11], ~and_27_out[12], ~and_27_out[13], ~and_27_out[14], ~and_27_out[15]);  // AND_Gate
  assign or_131_out = command_unit_mov_reg_reg_11_ram_instruction | or_132_out;  // OR_Gate or_131, 8 bits wide
  and mov_dx_bx (mov_dx_bx_out, and_27_out[0], and_27_out[1], and_27_out[2], and_27_out[3], ~and_27_out[4], ~and_27_out[5], ~and_27_out[6], ~and_27_out[7], ~and_27_out[8], ~and_27_out[9], ~and_27_out[10], ~and_27_out[11], ~and_27_out[12], ~and_27_out[13], ~and_27_out[14], ~and_27_out[15]);  // AND_Gate
  assign or_132_out = command_unit_mov_reg_reg_12_ram_instruction | or_133_out;  // OR_Gate or_132, 8 bits wide
  and mov_dx_cx (mov_dx_cx_out, ~and_27_out[0], ~and_27_out[1], ~and_27_out[2], ~and_27_out[3], and_27_out[4], ~and_27_out[5], ~and_27_out[6], ~and_27_out[7], ~and_27_out[8], ~and_27_out[9], ~and_27_out[10], ~and_27_out[11], ~and_27_out[12], ~and_27_out[13], ~and_27_out[14], ~and_27_out[15]);  // AND_Gate
  assign or_133_out = command_unit_mov_reg_reg_13_ram_instruction | or_134_out;  // OR_Gate or_133, 8 bits wide
  and mov_ax__ax (mov_ax__ax_out, and_27_out[0], ~and_27_out[1], ~and_27_out[2], ~and_27_out[3], and_27_out[4], ~and_27_out[5], ~and_27_out[6], ~and_27_out[7], ~and_27_out[8], ~and_27_out[9], ~and_27_out[10], ~and_27_out[11], ~and_27_out[12], ~and_27_out[13], ~and_27_out[14], ~and_27_out[15]);  // AND_Gate
  assign or_134_out = command_unit_mov_reg_reg_14_ram_instruction | or_135_out;  // OR_Gate or_134, 8 bits wide
  and mov_ax__bx (mov_ax__bx_out, ~and_27_out[0], and_27_out[1], ~and_27_out[2], ~and_27_out[3], and_27_out[4], ~and_27_out[5], ~and_27_out[6], ~and_27_out[7], ~and_27_out[8], ~and_27_out[9], ~and_27_out[10], ~and_27_out[11], ~and_27_out[12], ~and_27_out[13], ~and_27_out[14], ~and_27_out[15]);  // AND_Gate
  assign or_135_out = command_unit_mov_reg_reg_15_ram_instruction | or_136_out;  // OR_Gate or_135, 8 bits wide
  and mov_ax__cx (mov_ax__cx_out, and_27_out[0], and_27_out[1], ~and_27_out[2], ~and_27_out[3], and_27_out[4], ~and_27_out[5], ~and_27_out[6], ~and_27_out[7], ~and_27_out[8], ~and_27_out[9], ~and_27_out[10], ~and_27_out[11], ~and_27_out[12], ~and_27_out[13], ~and_27_out[14], ~and_27_out[15]);  // AND_Gate
  assign or_136_out = command_unit_mov_reg_reg_16_ram_instruction | or_137_out;  // OR_Gate or_136, 8 bits wide
  and mov_ax__dx (mov_ax__dx_out, ~and_27_out[0], ~and_27_out[1], and_27_out[2], ~and_27_out[3], and_27_out[4], ~and_27_out[5], ~and_27_out[6], ~and_27_out[7], ~and_27_out[8], ~and_27_out[9], ~and_27_out[10], ~and_27_out[11], ~and_27_out[12], ~and_27_out[13], ~and_27_out[14], ~and_27_out[15]);  // AND_Gate
  assign or_137_out = command_unit_mov_reg_reg_17_ram_instruction | or_138_out;  // OR_Gate or_137, 8 bits wide
  and mov_bx__ax (mov_bx__ax_out, and_27_out[0], ~and_27_out[1], and_27_out[2], ~and_27_out[3], and_27_out[4], ~and_27_out[5], ~and_27_out[6], ~and_27_out[7], ~and_27_out[8], ~and_27_out[9], ~and_27_out[10], ~and_27_out[11], ~and_27_out[12], ~and_27_out[13], ~and_27_out[14], ~and_27_out[15]);  // AND_Gate
  assign or_138_out = command_unit_mov_reg_reg_18_ram_instruction | or_139_out;  // OR_Gate or_138, 8 bits wide
  and mov_bx__bx (mov_bx__bx_out, ~and_27_out[0], and_27_out[1], and_27_out[2], ~and_27_out[3], and_27_out[4], ~and_27_out[5], ~and_27_out[6], ~and_27_out[7], ~and_27_out[8], ~and_27_out[9], ~and_27_out[10], ~and_27_out[11], ~and_27_out[12], ~and_27_out[13], ~and_27_out[14], ~and_27_out[15]);  // AND_Gate
  assign or_139_out = command_unit_mov_reg_reg_19_ram_instruction | or_140_out;  // OR_Gate or_139, 8 bits wide
  and mov_bx__cx (mov_bx__cx_out, and_27_out[0], and_27_out[1], and_27_out[2], ~and_27_out[3], and_27_out[4], ~and_27_out[5], ~and_27_out[6], ~and_27_out[7], ~and_27_out[8], ~and_27_out[9], ~and_27_out[10], ~and_27_out[11], ~and_27_out[12], ~and_27_out[13], ~and_27_out[14], ~and_27_out[15]);  // AND_Gate
  assign or_140_out = command_unit_mov_reg_reg_20_ram_instruction | or_141_out;  // OR_Gate or_140, 8 bits wide
  and mov_bx__dx (mov_bx__dx_out, ~and_27_out[0], ~and_27_out[1], ~and_27_out[2], and_27_out[3], and_27_out[4], ~and_27_out[5], ~and_27_out[6], ~and_27_out[7], ~and_27_out[8], ~and_27_out[9], ~and_27_out[10], ~and_27_out[11], ~and_27_out[12], ~and_27_out[13], ~and_27_out[14], ~and_27_out[15]);  // AND_Gate
  assign or_141_out = command_unit_mov_reg_reg_21_ram_instruction | or_142_out;  // OR_Gate or_141, 8 bits wide
  and mov_cx__ax (mov_cx__ax_out, and_27_out[0], ~and_27_out[1], ~and_27_out[2], and_27_out[3], and_27_out[4], ~and_27_out[5], ~and_27_out[6], ~and_27_out[7], ~and_27_out[8], ~and_27_out[9], ~and_27_out[10], ~and_27_out[11], ~and_27_out[12], ~and_27_out[13], ~and_27_out[14], ~and_27_out[15]);  // AND_Gate
  assign or_142_out = command_unit_mov_reg_reg_22_ram_instruction;  // OR_Gate or_142, 8 bits wide OR_Gate
  and mov_cx__bx (mov_cx__bx_out, ~and_27_out[0], and_27_out[1], ~and_27_out[2], and_27_out[3], and_27_out[4], ~and_27_out[5], ~and_27_out[6], ~and_27_out[7], ~and_27_out[8], ~and_27_out[9], ~and_27_out[10], ~and_27_out[11], ~and_27_out[12], ~and_27_out[13], ~and_27_out[14], ~and_27_out[15]);  // AND_Gate
  or or_143 (or_143_out, command_unit_mov_reg_value16_4_ram_enable, or_115_out);
  assign or_144_out = command_unit_mov_reg_value16_4_ram_instruction | or_116_out;  // OR_Gate or_144, 8 bits wide
  assign and_27_out = {16{and_26_out[15]}} & Data_In;  // AND_Gate and_27, 16 bits wide
  or or_145 (RAM0_Instruction_Enable, and_26_out[15], or_143_out);
  assign RAM0_Instruction = {3'b000, {2{and_26_out[15]}}, 3'b000} | or_144_out;  // OR_Gate or_146, 8 bits wide
endmodule
